// Logisim project Cdm8e-template.circ as structural Verilog: 1 circuit, main circuit main
module main (
);

  wire button_1_out, cdm_8e_1_p1, cdm_8e_1_p2, cdm_8e_1_p4, cdm_8e_1_p5, cdm_8e_1_p7, cdm_8e_1_p8,
       cdm_8e_1_p9, CL, code, data, mem, not_1_out, rd_wr_prime;
  wire [7:0] cdm_8e_1_p13, cdm_8e_1_p14, controlled_buffer_1_out;
  wire [15:0] cdm_8e_1_p12;

  // Probe on cdm_8e_1_p1
  // Probe on cdm_8e_1_p2
  // Probe on cdm_8e_1_p4
  Clock clock_1 (.out(CL));
  // Probe on cdm_8e_1_p7
  // Probe on cdm_8e_1_p8
  // Probe on cdm_8e_1_p5
  Button button_1 (.out(button_1_out));
  // CdM_8e cdm_8e_1: pin names not known; wires that end beside it: cdm_8e_1_p1, cdm_8e_1_p2, CL, cdm_8e_1_p4, cdm_8e_1_p5, button_1_out, cdm_8e_1_p7, cdm_8e_1_p8, cdm_8e_1_p9, mem, rd_wr_prime, cdm_8e_1_p12, cdm_8e_1_p13, cdm_8e_1_p14
  Decoder decoder_1 (.out0(code), .out1(data), .sel(cdm_8e_1_p9), .en(mem));
  assign controlled_buffer_1_out = not_1_out ? cdm_8e_1_p13 : 8'bz;  // Controlled_Buffer controlled_buffer_1
  not not_1 (not_1_out, rd_wr_prime);
  assign cdm_8e_1_p14 = rd_wr_prime ? controlled_buffer_1_out : 8'bz;  // Controlled_Buffer controlled_buffer_2
  ROM #(.addrWidth(16)) rom_1 (.addr(cdm_8e_1_p12), .data(controlled_buffer_1_out), .sel(code));
  RAM #(.addrWidth(16)) ram_1 (
    .addr(cdm_8e_1_p12), .data(controlled_buffer_1_out), .sel(data), .clk(CL), .ld(rd_wr_prime));  // open: clr

  // Notes on the sheet:
  //   contents of rom_1 (hex, n*v repeats v):
  //   d0 1 d1 2 d2 3 d3 4 d4
endmodule
