// Logisim project tennis_circ.circ as structural Verilog
module main (
  input  [4:0] in_1,
  input  [4:0] in_2
);

  wire clock, D, mem, not_1_out, or_1_out, read, t_ff_1_q, t_ff_2_q, t_ff_3_q, t_ff_4_q, U, vx_change, word;
  wire [2:0] x_8, y_8;
  wire [4:0] video_1_ball_x_2, video_1_ball_y_2, video_1_chip_id_2, video_1_left_bat_y_2,
       video_1_right_bat_y_2, video_2_ball_x_2, video_2_ball_y_2, video_2_chip_id_2, video_2_left_bat_y_2,
       video_2_right_bat_y_2, video_3_ball_x_2, video_3_ball_y_2, video_3_chip_id_2, video_3_left_bat_y_2,
       video_3_right_bat_y_2, x_5, y_5;
  wire [7:0] adder_1_out, adder_2_out, adder_3_out, multiplexer_1_out, multiplexer_2_out, multiplexer_3_out,
       multiplexer_4_out, multiplexer_5_out, multiplexer_6_out, neg_vx, register_1_q, subtractor_1_out,
       undriven, vx, vy_q;
  wire [15:0] address_bus, cdm16_1_p6, cdm16_1_p7, data_bus;
  wire [31:0] video_1_out_6, video_1_out_7, video_1_out_8, video_1_out_9, video_1_out_10, video_1_out_11,
       video_1_out_12, video_1_out_13, video_2_out_6, video_2_out_7, video_2_out_8, video_2_out_9,
       video_2_out_10, video_2_out_11, video_2_out_12, video_2_out_13, video_3_out_6, video_3_out_7,
       video_3_out_8, video_3_out_9, video_3_out_10, video_3_out_11, video_3_out_12, video_3_out_13,
       video_4_out_6, video_4_out_7, video_4_out_8, video_4_out_9, video_4_out_10, video_4_out_11,
       video_4_out_12, video_4_out_13;

  Clock clock_1 (.out(clock));
  // cdm16 cdm16_1: pin names not known; wires that end beside it: clock, mem, read, word, address_bus, cdm16_1_p6, cdm16_1_p7
  assign data_bus = not_1_out ? cdm16_1_p6 : 16'bz;  // Controlled_Buffer controlled_buffer_1
  not not_1 (not_1_out, read);
  assign cdm16_1_p7 = read ? data_bus : 16'bz;  // Controlled_Buffer controlled_buffer_2
  Adder adder_1 (.a(register_1_q), .b(8'h2), .out(adder_1_out));  // open: cin, cout
  Subtractor subtractor_1 (.a(register_1_q), .b(8'h2), .out(subtractor_1_out));  // open: bin, bout
  Multiplexer #(.width(8)) multiplexer_1 (
    .in0({8{1'b1}}), .in1(undriven), .out(multiplexer_1_out), .sel(t_ff_1_q));  // open: en
  T_Flip_Flop t_ff_1 (.clk(clock), .Q(t_ff_1_q), .preset(clock), .en(1'b1));  // open: T, Qn, reset
  Multiplexer #(.width(8)) multiplexer_2 (.in0(8'h1), .out(multiplexer_2_out), .sel(t_ff_2_q));  // open: in1, en
  T_Flip_Flop t_ff_2 (.clk(clock), .Q(t_ff_2_q), .preset(clock), .en(1'b1));  // open: T, Qn, reset
  Multiplexer #(.select(2), .width(8)) multiplexer_3 (
    .in0(register_1_q), .in1(adder_1_out), .in2(subtractor_1_out), .out(multiplexer_3_out), .sel({D, U}));  // open: in3, en
  Register register_1 (.D(multiplexer_3_out), .Q(register_1_q), .clk(clock));  // open: en, clr
  Register u_vx (.D(multiplexer_1_out), .Q(vx), .clk(clock));  // open: en, clr
  Register vy (.D(multiplexer_2_out), .Q(vy_q), .clk(clock));  // open: en, clr
  Adder adder_2 (.a({x_5, x_8}), .b(vx), .out(adder_2_out));  // open: cin, cout
  Multiplexer #(.width(8)) multiplexer_4 (
    .in0(8'h7f), .in1(adder_2_out), .out(multiplexer_4_out), .sel(t_ff_3_q));  // open: en
  T_Flip_Flop t_ff_3 (.clk(clock), .Q(t_ff_3_q), .preset(clock), .en(1'b1));  // open: T, Qn, reset
  Adder adder_3 (.a({y_5, y_8}), .b(vy_q), .out(adder_3_out));  // open: cin, cout
  Multiplexer #(.width(8)) multiplexer_5 (
    .in0(8'h7f), .in1(adder_3_out), .out(multiplexer_5_out), .sel(t_ff_4_q));  // open: en
  T_Flip_Flop t_ff_4 (.clk(clock), .Q(t_ff_4_q), .preset(clock), .en(1'b1));  // open: T, Qn, reset
  Register x (.D(multiplexer_4_out), .Q({x_5, x_8}), .clk(clock));  // open: en, clr
  Register y (.D(multiplexer_5_out), .Q({y_5, y_8}), .clk(clock));  // open: en, clr
  or or_1 (or_1_out, read, vx_change);
  // RAM ram_1: pin names not known; wires that end beside it: address_bus, word, mem, clock, or_1_out, data_bus
  Button u_U (.out(U));
  Button u_D (.out(D));
  DotMatrix #(.matrixcols(32), .matrixrows(32)) dotmatrix_1 (
    .col0(video_1_out_6), .col1(video_1_out_7), .col2(video_1_out_8), .col3(video_1_out_9),
    .col4(video_1_out_10), .col5(video_1_out_11), .col6(video_1_out_12), .col7(video_1_out_13),
    .col8(video_2_out_6), .col9(video_2_out_7), .col10(video_2_out_8), .col11(video_2_out_9),
    .col12(video_2_out_10), .col13(video_2_out_11), .col14(video_2_out_12), .col15(video_2_out_13),
    .col16(video_3_out_6), .col17(video_3_out_7), .col18(video_3_out_8), .col19(video_3_out_9),
    .col20(video_3_out_10), .col21(video_3_out_11), .col22(video_3_out_12), .col23(video_3_out_13),
    .col24(video_4_out_6), .col25(video_4_out_7), .col26(video_4_out_8), .col27(video_4_out_9),
    .col28(video_4_out_10), .col29(video_4_out_11), .col30(video_4_out_12), .col31(video_4_out_13));
  video video_1 (
    .Chip_ID(in_1), .Ball_X(x_5), .Ball_Y(y_5), .left_bat_Y(register_1_q[7:3]), .right_bat_Y(in_2),
    .Chip_ID_2(video_1_chip_id_2), .Ball_X_2(video_1_ball_x_2), .Ball_Y_2(video_1_ball_y_2),
    .left_bat_Y_2(video_1_left_bat_y_2), .right_bat_Y_2(video_1_right_bat_y_2), .out_6(video_1_out_6),
    .out_7(video_1_out_7), .out_8(video_1_out_8), .out_9(video_1_out_9), .out_10(video_1_out_10),
    .out_11(video_1_out_11), .out_12(video_1_out_12), .out_13(video_1_out_13));
  Comparator comparator_1 (.a({x_5, x_8}), .b({8{1'b1}}), .eq(vx_change));  // open: gt, lt
  Negator negator_1 (.in(vx), .out(neg_vx));
  video video_2 (
    .Chip_ID(video_1_chip_id_2), .Ball_X(video_1_ball_x_2), .Ball_Y(video_1_ball_y_2),
    .left_bat_Y(video_1_left_bat_y_2), .right_bat_Y(video_1_right_bat_y_2), .Chip_ID_2(video_2_chip_id_2),
    .Ball_X_2(video_2_ball_x_2), .Ball_Y_2(video_2_ball_y_2), .left_bat_Y_2(video_2_left_bat_y_2),
    .right_bat_Y_2(video_2_right_bat_y_2), .out_6(video_2_out_6), .out_7(video_2_out_7),
    .out_8(video_2_out_8), .out_9(video_2_out_9), .out_10(video_2_out_10), .out_11(video_2_out_11),
    .out_12(video_2_out_12), .out_13(video_2_out_13));
  video video_3 (
    .Chip_ID(video_2_chip_id_2), .Ball_X(video_2_ball_x_2), .Ball_Y(video_2_ball_y_2),
    .left_bat_Y(video_2_left_bat_y_2), .right_bat_Y(video_2_right_bat_y_2), .Chip_ID_2(video_3_chip_id_2),
    .Ball_X_2(video_3_ball_x_2), .Ball_Y_2(video_3_ball_y_2), .left_bat_Y_2(video_3_left_bat_y_2),
    .right_bat_Y_2(video_3_right_bat_y_2), .out_6(video_3_out_6), .out_7(video_3_out_7),
    .out_8(video_3_out_8), .out_9(video_3_out_9), .out_10(video_3_out_10), .out_11(video_3_out_11),
    .out_12(video_3_out_12), .out_13(video_3_out_13));
  Multiplexer #(.width(8)) multiplexer_6 (
    .in0(vx), .in1(neg_vx), .out(multiplexer_6_out), .sel(vx_change));  // open: en
  video video_4 (
    .Chip_ID(video_3_chip_id_2), .Ball_X(video_3_ball_x_2), .Ball_Y(video_3_ball_y_2),
    .left_bat_Y(video_3_left_bat_y_2), .right_bat_Y(video_3_right_bat_y_2), .out_6(video_4_out_6),
    .out_7(video_4_out_7), .out_8(video_4_out_8), .out_9(video_4_out_9), .out_10(video_4_out_10),
    .out_11(video_4_out_11), .out_12(video_4_out_12), .out_13(video_4_out_13));  // open: Chip_ID_2, Ball_X_2, Ball_Y_2, left_bat_Y_2, right_bat_Y_2

  // Other names for the same wires on the sheet: x_8[7:3] = x_5; y_8[7:3] = y_5
endmodule

module video (
  input  [4:0] Chip_ID,
  input  [4:0] Ball_X,
  input  [4:0] Ball_Y,
  input  [4:0] left_bat_Y,
  input  [4:0] right_bat_Y,
  output [31:0] out_6,
  output [31:0] out_7,
  output [31:0] out_8,
  output [31:0] out_9,
  output [31:0] out_10,
  output [31:0] out_11,
  output [31:0] out_12,
  output [31:0] out_13,
  output [4:0] Chip_ID_2,
  output [4:0] Ball_X_2,
  output [4:0] Ball_Y_2,
  output [4:0] left_bat_Y_2,
  output [4:0] right_bat_Y_2
);

  wire comparator_1_eq, comparator_2_eq, comparator_3_eq, comparator_4_eq, comparator_5_eq, comparator_6_eq,
       comparator_7_eq, comparator_8_eq, comparator_9_eq, comparator_10_eq;
  wire [4:0] id_1, id_2, id_3, id_4, id_5, id_6, id_7, video_chip_1_out_7, video_chip_1_out_8,
       video_chip_1_out_9, video_chip_1_out_10, video_chip_2_out_7, video_chip_2_out_8, video_chip_2_out_9,
       video_chip_2_out_10, video_chip_3_out_7, video_chip_3_out_8, video_chip_3_out_9, video_chip_3_out_10,
       video_chip_4_out_7, video_chip_4_out_8, video_chip_4_out_9, video_chip_4_out_10, video_chip_5_out_7,
       video_chip_5_out_8, video_chip_5_out_9, video_chip_5_out_10, video_chip_6_out_7, video_chip_6_out_8,
       video_chip_6_out_9, video_chip_6_out_10, video_chip_7_out_7, video_chip_7_out_8, video_chip_7_out_9,
       video_chip_7_out_10;
  wire [31:0] BALLS_OUT, l_bat_out, multiplexer_1_out, multiplexer_2_out, multiplexer_9_out,
       multiplexer_10_out, r_bat_out;

  Multiplexer #(.width(32)) multiplexer_1 (
    .in0({32{1'b0}}), .in1(l_bat_out), .out(multiplexer_1_out), .sel(comparator_1_eq));  // open: en
  Comparator #(.width(5)) comparator_1 (.a(Chip_ID), .b({5{1'b0}}), .eq(comparator_1_eq));  // open: gt, lt
  assign out_6 = multiplexer_1_out | multiplexer_2_out;  // OR_Gate or_1, 32 bits wide
  Multiplexer #(.width(32)) multiplexer_2 (
    .in0({32{1'b0}}), .in1(BALLS_OUT), .out(multiplexer_2_out), .sel(comparator_2_eq));  // open: en
  Comparator #(.width(5)) comparator_2 (.a(Chip_ID), .b(Ball_X), .eq(comparator_2_eq));  // open: gt, lt
  video_chip video_chip_1 (
    .Chip_id(Chip_ID), .Ball_X(Ball_X), .Ball_Y(Ball_Y), .left_bat_X(left_bat_Y), .right_bat_Y(right_bat_Y),
    .out_6(id_1), .out_7(video_chip_1_out_7), .out_8(video_chip_1_out_8), .out_9(video_chip_1_out_9),
    .out_10(video_chip_1_out_10));
  Multiplexer #(.width(32)) multiplexer_3 (
    .in0({32{1'b0}}), .in1(BALLS_OUT), .out(out_7), .sel(comparator_3_eq));  // open: en
  Comparator #(.width(5)) comparator_3 (.a(id_1), .b(Ball_X), .eq(comparator_3_eq));  // open: gt, lt
  video_chip video_chip_2 (
    .Chip_id(id_1), .Ball_X(video_chip_1_out_7), .Ball_Y(video_chip_1_out_8),
    .left_bat_X(video_chip_1_out_9), .right_bat_Y(video_chip_1_out_10), .out_6(id_2),
    .out_7(video_chip_2_out_7), .out_8(video_chip_2_out_8), .out_9(video_chip_2_out_9),
    .out_10(video_chip_2_out_10));
  Multiplexer #(.width(32)) multiplexer_4 (
    .in0({32{1'b0}}), .in1(BALLS_OUT), .out(out_8), .sel(comparator_4_eq));  // open: en
  Comparator #(.width(5)) comparator_4 (.a(id_2), .b(Ball_X), .eq(comparator_4_eq));  // open: gt, lt
  Shifter #(.width(32)) shifter_1 (.in(32'h1), .\dist (Ball_Y), .out(BALLS_OUT));
  video_chip video_chip_3 (
    .Chip_id(id_2), .Ball_X(video_chip_2_out_7), .Ball_Y(video_chip_2_out_8),
    .left_bat_X(video_chip_2_out_9), .right_bat_Y(video_chip_2_out_10), .out_6(id_3),
    .out_7(video_chip_3_out_7), .out_8(video_chip_3_out_8), .out_9(video_chip_3_out_9),
    .out_10(video_chip_3_out_10));
  Multiplexer #(.width(32)) multiplexer_5 (
    .in0({32{1'b0}}), .in1(BALLS_OUT), .out(out_9), .sel(comparator_5_eq));  // open: en
  Comparator #(.width(5)) comparator_5 (.a(id_3), .b(Ball_X), .eq(comparator_5_eq));  // open: gt, lt
  video_chip video_chip_4 (
    .Chip_id(id_3), .Ball_X(video_chip_3_out_7), .Ball_Y(video_chip_3_out_8),
    .left_bat_X(video_chip_3_out_9), .right_bat_Y(video_chip_3_out_10), .out_6(id_4),
    .out_7(video_chip_4_out_7), .out_8(video_chip_4_out_8), .out_9(video_chip_4_out_9),
    .out_10(video_chip_4_out_10));
  Multiplexer #(.width(32)) multiplexer_6 (
    .in0({32{1'b0}}), .in1(BALLS_OUT), .out(out_10), .sel(comparator_6_eq));  // open: en
  Comparator #(.width(5)) comparator_6 (.a(id_4), .b(Ball_X), .eq(comparator_6_eq));  // open: gt, lt
  video_chip video_chip_5 (
    .Chip_id(id_4), .Ball_X(video_chip_4_out_7), .Ball_Y(video_chip_4_out_8),
    .left_bat_X(video_chip_4_out_9), .right_bat_Y(video_chip_4_out_10), .out_6(id_5),
    .out_7(video_chip_5_out_7), .out_8(video_chip_5_out_8), .out_9(video_chip_5_out_9),
    .out_10(video_chip_5_out_10));
  Shifter #(.width(32)) shifter_2 (.in(32'hf), .\dist (left_bat_Y), .out(l_bat_out));
  Shifter #(.width(32)) shifter_3 (.in(32'hf), .\dist (right_bat_Y), .out(r_bat_out));
  Multiplexer #(.width(32)) multiplexer_7 (
    .in0({32{1'b0}}), .in1(BALLS_OUT), .out(out_11), .sel(comparator_7_eq));  // open: en
  Comparator #(.width(5)) comparator_7 (.a(id_5), .b(Ball_X), .eq(comparator_7_eq));  // open: gt, lt
  video_chip video_chip_6 (
    .Chip_id(id_5), .Ball_X(video_chip_5_out_7), .Ball_Y(video_chip_5_out_8),
    .left_bat_X(video_chip_5_out_9), .right_bat_Y(video_chip_5_out_10), .out_6(id_6),
    .out_7(video_chip_6_out_7), .out_8(video_chip_6_out_8), .out_9(video_chip_6_out_9),
    .out_10(video_chip_6_out_10));
  Multiplexer #(.width(32)) multiplexer_8 (
    .in0({32{1'b0}}), .in1(BALLS_OUT), .out(out_12), .sel(comparator_8_eq));  // open: en
  Comparator #(.width(5)) comparator_8 (.a(id_6), .b(Ball_X), .eq(comparator_8_eq));  // open: gt, lt
  video_chip video_chip_7 (
    .Chip_id(id_6), .Ball_X(video_chip_6_out_7), .Ball_Y(video_chip_6_out_8),
    .left_bat_X(video_chip_6_out_9), .right_bat_Y(video_chip_6_out_10), .out_6(id_7),
    .out_7(video_chip_7_out_7), .out_8(video_chip_7_out_8), .out_9(video_chip_7_out_9),
    .out_10(video_chip_7_out_10));
  video_chip video_chip_8 (
    .Chip_id(id_7), .Ball_X(video_chip_7_out_7), .Ball_Y(video_chip_7_out_8),
    .left_bat_X(video_chip_7_out_9), .right_bat_Y(video_chip_7_out_10), .out_6(Chip_ID_2), .out_7(Ball_X_2),
    .out_8(Ball_Y_2), .out_9(left_bat_Y_2), .out_10(right_bat_Y_2));
  assign out_13 = multiplexer_9_out | multiplexer_10_out;  // OR_Gate or_2, 32 bits wide
  Multiplexer #(.width(32)) multiplexer_9 (
    .in0({32{1'b0}}), .in1(BALLS_OUT), .out(multiplexer_9_out), .sel(comparator_9_eq));  // open: en
  Comparator #(.width(5)) comparator_9 (.a(id_7), .b(Ball_X), .eq(comparator_9_eq));  // open: gt, lt
  Multiplexer #(.width(32)) multiplexer_10 (
    .in0({32{1'b0}}), .in1(r_bat_out), .out(multiplexer_10_out), .sel(comparator_10_eq));  // open: en
  Comparator #(.width(5)) comparator_10 (.a({5{1'b1}}), .b(id_7), .eq(comparator_10_eq));  // open: gt, lt

  // Other names for the same wires on the sheet: id_0[4:0] = Chip_ID; l_bat[4:0] = left_bat_Y;
  //   r_bat[4:0] = right_bat_Y; x[4:0] = Ball_X; y[4:0] = Ball_Y

  // Notes on the sheet:
  //   0
  //   1
  //   2
  //   3
  //   4
  //   5
  //   6
  //   7
endmodule

module video_chip (
  input  [4:0] Chip_id,
  input  [4:0] Ball_X,
  input  [4:0] Ball_Y,
  input  [4:0] left_bat_X,
  input  [4:0] right_bat_Y,
  output [4:0] out_6,
  output [4:0] out_7,
  output [4:0] out_8,
  output [4:0] out_9,
  output [4:0] out_10
);

  Adder #(.width(5)) adder_1 (.a(5'b00001), .b(Chip_id), .out(out_6));  // open: cin, cout

  assign out_7 = Ball_X;
  assign out_8 = Ball_Y;
  assign out_9 = left_bat_X;
  assign out_10 = right_bat_Y;
endmodule
