// Logisim project pohuy+pohuy.circ as structural Verilog: 2 circuits, main circuit main
module main (
  input  in_1,
  output out_2,
  output out_3
);

  wire cdm16_1_p1, cdm16_1_p3, clock, code, comparator_1_eq, data, mem, not_1_out, read, word;
  wire [7:0] ext_data, vec_adr;
  wire [15:0] address_bus, cdm16_1_p8, cdm16_1_p9, data_bus;
  wire [15:8] multiplexer_1_out;

  Clock clock_1 (.out(clock));
  // Probe on cdm16_1_p1
  // cdm16 cdm16_1: pin names not known; wires that end beside it: cdm16_1_p1, clock, cdm16_1_p3, mem, read, word, address_bus, cdm16_1_p8, cdm16_1_p9
  assign cdm16_1_p9 = read ? data_bus : 16'bz;  // Controlled_Buffer controlled_buffer_1
  Multiplexer #(.width(16)) multiplexer_1 (
    .in0({16{1'b0}}), .in1(data_bus), .out({multiplexer_1_out, ext_data}), .sel(comparator_1_eq));  // open: en
  Comparator #(.width(16)) comparator_1 (.a(address_bus), .b(16'h1), .eq(comparator_1_eq));  // open: gt, lt
  Decoder decoder_1 (.out0(code), .out1(data), .sel(cdm16_1_p3), .en(mem));
  assign data_bus = not_1_out ? cdm16_1_p8 : 16'bz;  // Controlled_Buffer controlled_buffer_2
  not not_1 (not_1_out, read);
  // ROM rom_1: pin names not known; wires that end beside it: address_bus, code, word, data_bus
  // RAM ram_1: pin names not known; wires that end beside it: address_bus, word, data, clock, read, data_bus
  // UART uart_1: pin names not known; wires that end beside it: vec_adr, ext_data, out_2, clock, in_1, out_3, 1'b1
endmodule

module _0_0_1 (
);

  wire comparator_1_eq;
  wire [7:0] ext_data;
  wire [15:0] address_bus, data_bus;
  wire [15:8] multiplexer_1_out;

  Comparator #(.width(16)) comparator_1 (.a(address_bus), .b(16'hff), .eq(comparator_1_eq));  // open: gt, lt
  Multiplexer #(.width(16)) multiplexer_1 (
    .in0({16{1'b0}}), .in1(data_bus), .out({multiplexer_1_out, ext_data}), .sel(comparator_1_eq));  // open: en
endmodule
