// Logisim project pohuy.circ as structural Verilog: 6 circuits, main circuit main
// C:\Ass_project\poker\out.img
module main (
  output out_1,
  output out_2
);

  wire block, \break , cdm_16_1_p1, clk, clock, comparator_1_eq, comparator_2_eq, comparator_3_eq,
       comparator_4_eq, comparator_5_eq, comparator_6_eq, comparator_7_eq, comparator_8_eq, comparator_9_eq,
       comparator_10_eq, comparator_11_eq, comparator_12_eq, comparator_13_eq, comparator_14_eq,
       comparator_15_eq, comparator_16_eq, comparator_17_eq, comparator_18_eq, comparator_18_gt,
       comparator_18_lt, from_break, from_signal, mem, multiplexer_2_out, multiplexer_6_out,
       multiplexer_7_out, multiplexer_8_out, multiplexer_10_out, not_1_out, not_2_out, or_2_out,
       pull_resistor_1_node, pull_resistor_7_node, ram_1_p5, read, register_1_q, register_4_q, start, telnet,
       transistor_14_out, uart_1_p5, word, wr_rd;
  wire [5:0] _1r, _2r, _3r, _4r, _5r, _6r, _7r, _8r, _9r, _10r, _11r, _12r, _13r, _14r, _15r, _16r, _17r,
       _18r, _19r, _20r, _21r, _22r, _23r, _24r, _25r, _26r, _27r, _28r, _29r, _30r, in_memory,
       randome_numbers_1_in_memory;
  wire [7:0] ext_data, undriven, vec_adr;
  wire [15:0] adder_1_out, adder_2_out, adder_3_out, address_bus, cdm_16_1_p5, cdm_16_1_p6, cdm_16_1_p7,
       command, controlled_buffer_2_out, data_bus, from, how_much, multiplexer_5_out, multiplexer_11_out,
       multiplexer_12_out, multiplexer_13_out, multiplexer_14_out, multiplexer_15_out, multiplexer_16_out,
       multiplexer_17_out, multiplexer_18_out, multiplexer_19_out, multiplexer_20_out, multiplexer_21_out,
       multiplexer_22_out, multiplexer_23_out, multiplexer_24_out, multiplexer_25_out, multiplexer_26_out,
       multiplexer_27_out, multiplexer_28_out, multiplexer_29_out, multiplexer_30_out, num,
       pull_resistor_6_node, register_3_q, register_5_q, register_7_q, register_8_q, register_9_q,
       register_10_q, register_11_q, register_12_q, register_16_q, temporary_data, transistor_3_out,
       transistor_4_out;
  wire [15:8] transistor_13_out;

  // Debugger debugger_1: pin names not known
  // CdM_16 cdm_16_1: pin names not known; wires that end beside it: cdm_16_1_p1, mem, read, word, cdm_16_1_p5, cdm_16_1_p6, cdm_16_1_p7
  Multiplexer multiplexer_1 (.in0(multiplexer_2_out), .in1(1'b0), .out(cdm_16_1_p1), .sel(from_signal));  // open: en
  Multiplexer multiplexer_2 (.in0(clock), .in1(1'b0), .out(multiplexer_2_out), .sel(\break ));  // open: en
  // UART uart_1: pin names not known; wires that end beside it: vec_adr, ext_data, out_1, clock, uart_1_p5, out_2, 1'b1
  Comparator comparator_1 (.a(vec_adr), .b(8'ha), .eq(comparator_1_eq));  // open: gt, lt
  assign cdm_16_1_p7 = read ? multiplexer_5_out : 16'bz;  // Controlled_Buffer controlled_buffer_1
  or or_1 (uart_1_p5, comparator_1_eq, wr_rd);
  Comparator comparator_2 (.a(vec_adr), .b({8{1'b0}}), .eq(comparator_2_eq));  // open: gt, lt
  Multiplexer #(.width(16)) multiplexer_3 (.in0(cdm_16_1_p5), .out(address_bus), .sel(\break ));  // open: in1, en
  assign controlled_buffer_2_out = not_1_out ? cdm_16_1_p6 : 16'bz;  // Controlled_Buffer controlled_buffer_2
  not not_1 (not_1_out, read);
  // Probe on num
  Bid bid_1 (.in_3(vec_adr), .out_4(num), .in_2(clock), .in_1(comparator_3_eq));
  Comparator comparator_3 (.a(vec_adr), .b({8{1'b0}}), .eq(comparator_3_eq));  // open: gt, lt
  Pull_Resistor pull_resistor_1 (.node(pull_resistor_1_node));
  Transistor transistor_1 (.in(comparator_2_eq), .out(pull_resistor_1_node), .gate(block));
  Pull_Resistor pull_resistor_2 (.node(telnet));
  Transistor #(.\type ("n")) transistor_2 (.in(1'b1), .out(telnet), .gate(pull_resistor_1_node));
  Multiplexer #(.width(16)) multiplexer_4 (
    .in0(controlled_buffer_2_out), .in1(temporary_data), .out(data_bus), .sel(\break ));  // open: en
  Multiplexer #(.width(16)) multiplexer_5 (.in0(data_bus), .out(multiplexer_5_out), .sel(\break ));  // open: in1, en
  // Probe on address_bus
  Multiplexer multiplexer_6 (.in0(word), .in1(1'b1), .out(multiplexer_6_out), .sel(\break ));  // open: en
  Multiplexer multiplexer_7 (
    .in0(multiplexer_8_out), .in1(1'b1), .out(multiplexer_7_out), .sel(from_break));  // open: en
  Multiplexer multiplexer_8 (.in0(mem), .in1(not_2_out), .out(multiplexer_8_out), .sel(\break ));  // open: en
  not not_2 (not_2_out, register_1_q);
  Comparator comparator_4 (.a(vec_adr), .b(8'hd), .eq(comparator_4_eq));  // open: gt, lt
  // RAM ram_1: pin names not known; wires that end beside it: address_bus, multiplexer_6_out, multiplexer_7_out, clock, ram_1_p5, data_bus
  Multiplexer multiplexer_9 (.in0(multiplexer_10_out), .in1(1'b1), .out(ram_1_p5), .sel(from_break));  // open: en
  Multiplexer multiplexer_10 (.in0(read), .in1(register_1_q), .out(multiplexer_10_out), .sel(\break ));  // open: en
  Register #(.width(1)) register_1 (.D(telnet), .Q(register_1_q), .clk(clock));  // open: en, clr
  Multiplexer #(.width(16)) multiplexer_11 (
    .in0(command), .in1(num), .out(multiplexer_11_out), .sel(comparator_4_eq));  // open: en
  Multiplexer #(.width(16)) multiplexer_12 (
    .in0(16'hfc08), .in1(16'hfc0a), .out(multiplexer_12_out), .sel(comparator_4_eq));  // open: en
  Comparator #(.width(16)) comparator_5 (.a(address_bus), .b(16'hfc00), .eq(comparator_5_eq));  // open: gt, lt
  Multiplexer #(.width(16)) multiplexer_13 (
    .in0(multiplexer_11_out), .in1({16{1'b0}}), .out(multiplexer_13_out), .sel(comparator_6_eq));  // open: en
  Comparator comparator_6 (.a(vec_adr), .b(8'ha), .eq(comparator_6_eq));  // open: gt, lt
  Multiplexer #(.width(16)) multiplexer_14 (
    .in0(multiplexer_12_out), .in1(16'hfc00), .out(multiplexer_14_out), .sel(comparator_6_eq));  // open: en
  Multiplexer #(.width(16)) multiplexer_15 (
    .in0(register_3_q), .in1(data_bus), .out(multiplexer_15_out), .sel(comparator_7_eq));  // open: en
  Comparator #(.width(16)) comparator_7 (.a(address_bus), .b(16'hfc0c), .eq(comparator_7_eq));  // open: gt, lt
  Multiplexer #(.width(16)) multiplexer_16 (
    .in0({{15{1'b0}}, wr_rd}), .in1(data_bus), .out(multiplexer_16_out), .sel(comparator_5_eq));  // open: en
  Register #(.width(1)) register_2 (.D(multiplexer_16_out[0]), .Q(wr_rd), .clk(clock));  // open: en, clr
  // Probe on command
  Commands commands_1 (.intput_value(vec_adr), .output_value(command), .clock(clock));
  Transistor #(.width(16)) transistor_3 (.in(multiplexer_17_out), .out(transistor_3_out), .gate(block));
  Multiplexer #(.width(16)) multiplexer_17 (
    .in1(multiplexer_13_out), .out(multiplexer_17_out), .sel(\break ));  // open: in0, en
  Multiplexer #(.width(16)) multiplexer_18 (
    .in1(multiplexer_14_out), .out(multiplexer_18_out), .sel(\break ));  // open: in0, en
  Transistor #(.width(16)) transistor_4 (.in(multiplexer_18_out), .out(transistor_4_out), .gate(block));
  Register #(.width(16)) register_3 (.D(multiplexer_15_out), .Q(register_3_q), .clk(clock));  // open: en, clr
  Transistor #(.\type ("n")) transistor_5 (.in(1'b1), .out(\break ), .gate(wr_rd));
  Pull_Resistor pull_resistor_3 (.node(\break ));
  Transistor #(.width(16)) transistor_6 (.in(transistor_3_out), .out(data_bus), .gate(from_signal));
  Transistor #(.width(16)) transistor_7 (.in(transistor_4_out), .out(address_bus), .gate(from_signal));
  // Probe on register_3_q
  Comparator #(.width(16)) comparator_8 (.a(address_bus), .b(16'hfc0e), .eq(comparator_8_eq));  // open: gt, lt
  Pull_Resistor pull_resistor_4 (.node(ext_data));
  Register #(.width(1)) register_4 (.D(1'b1), .Q(register_4_q), .clk(clk));  // open: en, clr
  Register #(.width(16)) register_5 (.D(multiplexer_19_out), .Q(register_5_q), .clk(clock));  // open: en, clr
  Multiplexer #(.width(16)) multiplexer_19 (
    .in0(register_5_q), .in1(data_bus), .out(multiplexer_19_out), .sel(comparator_8_eq));  // open: en
  Multiplexer #(.width(16)) multiplexer_20 (
    .in0(register_7_q), .in1(data_bus), .out(multiplexer_20_out), .sel(comparator_9_eq));  // open: en
  Comparator #(.width(16)) comparator_9 (.a(address_bus), .b(16'hfc10), .eq(comparator_9_eq));  // open: gt, lt
  Transistor #(.\type ("n")) transistor_8 (.in(clk), .out(clock), .gate(start));
  Pull_Resistor pull_resistor_5 (.node(clock));
  Register #(.width(1)) register_6 (.D(register_4_q), .Q(start), .clk(clk));  // open: en, clr
  Clock clock_1 (.out(clk));
  // Probe on register_5_q
  Register #(.width(16)) register_7 (.D(multiplexer_20_out), .Q(register_7_q), .clk(clock));  // open: en, clr
  // Probe on register_7_q
  // Probe on _1r
  Multiplexer #(.width(16)) multiplexer_21 (
    .in0(register_8_q), .in1(data_bus), .out(multiplexer_21_out), .sel(comparator_10_eq));  // open: en
  Comparator #(.width(16)) comparator_10 (.a(address_bus), .b(16'hfc04), .eq(comparator_10_eq));  // open: gt, lt
  Comparator #(.width(16)) comparator_11 (.a(address_bus), .b(16'hfc12), .eq(comparator_11_eq));  // open: gt, lt
  // Probe on _4r
  // Probe on _3r
  // Probe on _2r
  // Probe on _5r
  Register #(.width(16)) register_8 (.D(multiplexer_21_out), .Q(register_8_q), .clk(clock));  // open: en, clr
  Register #(.width(16)) register_9 (.D(multiplexer_22_out), .Q(register_9_q), .clk(clock));  // open: en, clr
  Multiplexer #(.width(16)) multiplexer_22 (
    .in0(register_9_q), .in1(data_bus), .out(multiplexer_22_out), .sel(comparator_11_eq));  // open: en
  // Probe on _9r
  // Probe on _6r
  // Probe on _8r
  // Probe on _7r
  // Probe on register_8_q
  // Probe on register_9_q
  // Probe on _10r
  // Probe on _11r
  // Probe on _12r
  // Probe on _13r
  Comparator #(.width(16)) comparator_12 (.a(16'h7bc), .b(register_10_q), .eq(comparator_12_eq));  // open: gt, lt
  // Probe on multiplexer_23_out
  Adder #(.width(16)) adder_1 (.a(register_10_q), .b(16'h1), .out(adder_1_out));  // open: cin, cout
  Multiplexer #(.width(16)) multiplexer_23 (
    .in0(adder_1_out), .in1(register_10_q), .out(multiplexer_23_out), .sel(comparator_12_eq));  // open: en
  Comparator #(.width(16)) comparator_13 (.a(address_bus), .b(16'hfc06), .eq(comparator_13_eq));  // open: gt, lt
  Comparator #(.width(16)) comparator_14 (.a(address_bus), .b(16'hfc14), .eq(comparator_14_eq));  // open: gt, lt
  // Probe on _17r
  // Probe on _16r
  // Probe on _15r
  // Probe on _14r
  Random_store random_store_1 (
    .in_memory(in_memory), .random_address(16'hfe00), .\break (\break ), .data_bus(data_bus),
    .address_bus(address_bus), .block(block), .clk(clk));
  Register #(.width(16)) register_10 (.D(multiplexer_23_out), .Q(register_10_q), .clk(clock));  // open: en, clr
  Multiplexer #(.width(16)) multiplexer_24 (
    .in0(register_11_q), .in1(data_bus), .out(multiplexer_24_out), .sel(comparator_13_eq));  // open: en
  Register #(.width(16)) register_11 (.D(multiplexer_24_out), .Q(register_11_q), .clk(clock));  // open: en, clr
  Multiplexer #(.width(16)) multiplexer_25 (
    .in0(register_12_q), .in1(data_bus), .out(multiplexer_25_out), .sel(comparator_14_eq));  // open: en
  Register #(.width(16)) register_12 (.D(multiplexer_25_out), .Q(register_12_q), .clk(clock));  // open: en, clr
  // Probe on _19r
  // Probe on _18r
  // Probe on _20r
  // Probe on _21r
  // Probe on register_11_q
  // Probe on register_12_q
  // Probe on _24r
  // Probe on _25r
  // Probe on _22r
  // Probe on _23r
  Randome_numbers randome_numbers_1 (
    .in_1(clock), .out_2(_1r), .out_3(_2r), .out_4(_3r), .out_6(_4r), .out_7(_5r), .out_8(_6r), .out_9(_7r),
    .out_10(_8r), .out_11(_9r), .out_12(_10r), .out_13(_11r), .out_14(_12r), .out_15(_13r), .out_16(_14r),
    .out_17(_15r), .out_18(_16r), .out_19(_17r), .out_20(_18r), .out_21(_19r), .out_22(_20r), .out_23(_21r),
    .out_24(_22r), .out_25(_23r), .out_26(_24r), .out_27(_25r), .out_28(_26r), .out_29(_27r), .out_30(_28r),
    .out_31(_29r), .out_32(_30r), .in_memory(randome_numbers_1_in_memory));
  // ROM rom_1: pin names not known; wires that end beside it: register_10_q, 1'b1
  // Probe on _26r
  // Probe on _27r
  // Probe on _29r
  // Probe on _28r
  // Probe on in_memory
  Register #(.width(6)) register_13 (.D(randome_numbers_1_in_memory), .Q(in_memory), .clk(clock));  // open: en, clr
  // Probe on ext_data
  Transistor #(.width(8)) transistor_9 (.in(undriven), .out(ext_data), .gate(comparator_12_eq));
  // Probe on _30r
  Comparator #(.width(16)) comparator_15 (.a(address_bus), .b(16'hfc1a), .eq(comparator_15_eq));  // open: gt, lt
  Comparator #(.width(16)) comparator_16 (.a(address_bus), .b(16'hfc1c), .eq(comparator_16_eq));  // open: gt, lt
  Multiplexer #(.width(16)) multiplexer_26 (
    .in0(from), .in1(multiplexer_27_out), .out(multiplexer_26_out), .sel(comparator_15_eq));  // open: en
  Multiplexer #(.width(16)) multiplexer_27 (
    .in0({16{1'b0}}), .in1(data_bus), .out(multiplexer_27_out), .sel(comparator_15_eq));  // open: en
  Multiplexer #(.width(16)) multiplexer_28 (
    .in0(how_much), .in1(multiplexer_29_out), .out(multiplexer_28_out), .sel(comparator_16_eq));  // open: en
  Multiplexer #(.width(16)) multiplexer_29 (
    .in0({16{1'b0}}), .in1(data_bus), .out(multiplexer_29_out), .sel(comparator_16_eq));  // open: en
  Register #(.width(16)) register_14 (.D(multiplexer_26_out), .Q(from), .clk(clock));  // open: en, clr
  Register #(.width(16)) register_15 (.D(multiplexer_28_out), .Q(how_much), .clk(clock));  // open: en, clr
  Comparator #(.width(16), .mode("unsigned")) comparator_17 (
    .a({16{1'b0}}), .b(how_much), .eq(comparator_17_eq));  // open: gt, lt
  Pull_Resistor pull_resistor_6 (.node(pull_resistor_6_node));
  Adder #(.width(16)) adder_2 (.a(pull_resistor_6_node), .b(16'h2), .out(adder_2_out));  // open: cin, cout
  not not_3 (from_signal, comparator_17_eq);
  Transistor #(.\type ("n"), .width(16)) transistor_10 (
    .in(register_16_q), .out(pull_resistor_6_node), .gate(from_break));
  Adder #(.width(16)) adder_3 (.a(from), .b(how_much), .out(adder_3_out));  // open: cin, cout
  Comparator #(.width(16), .mode("unsigned")) comparator_18 (
    .a(adder_3_out), .b(register_16_q), .gt(comparator_18_gt), .eq(comparator_18_eq), .lt(comparator_18_lt));
  Register #(.width(16)) register_16 (.D(multiplexer_30_out), .Q(register_16_q), .clk(clock));  // open: en, clr
  Multiplexer #(.width(16)) multiplexer_30 (
    .in0(from), .in1(adder_2_out), .out(multiplexer_30_out), .sel(from_signal));  // open: en
  and and_1 (from_break, from_signal, comparator_18_gt);
  or or_2 (or_2_out, comparator_18_eq, comparator_18_lt);
  Transistor #(.\type ("n"), .width(16)) transistor_11 (.in(register_16_q), .out(address_bus), .gate(from_break));
  Pull_Resistor pull_resistor_7 (.node(pull_resistor_7_node));
  Transistor #(.\type ("n")) transistor_12 (.in(or_2_out), .out(pull_resistor_7_node), .gate(from_signal));
  Transistor #(.\type ("n"), .width(16)) transistor_13 (
    .in(data_bus), .out({transistor_13_out, ext_data}), .gate(from_break));
  Transistor transistor_14 (.in(pull_resistor_7_node), .out(transistor_14_out), .gate(block));
  Transistor #(.\type ("n"), .width(16)) transistor_15 (.in(16'hfc1c), .out(address_bus), .gate(transistor_14_out));
  // Probe on ext_data
  Pull_Resistor pull_resistor_8 (.node(transistor_14_out));
  Transistor #(.\type ("n"), .width(16)) transistor_16 (.in({16{1'b0}}), .out(data_bus), .gate(transistor_14_out));
  Transistor #(.\type ("n")) transistor_17 (.in(from_signal), .out(\break ), .gate(from_signal));
  Transistor #(.\type ("n")) transistor_18 (.in(1'b1), .out(telnet), .gate(transistor_14_out));

  // Notes on the sheet:
  //   BALANCE_BOT
  //   BALANCE_PLAYER
  //   ставка бота
  //   комбинация бота
  //   ставка игрока
  //   комбинация игрока
  //   Сдался
endmodule

module Commands (
  input  [7:0] intput_value,
  input  clock,
  output [15:0] output_value
);

  wire comparator_1_eq, comparator_2_eq, comparator_3_eq, comparator_4_eq, comparator_5_eq, comparator_6_eq,
       not_1_out, not_2_out;
  wire [7:0] bet, call, check, fold, multiplexer_6_out, or_1_out, pull_resistor_1_node, pull_resistor_2_node,
       pull_resistor_3_node, pull_resistor_4_node, pull_resistor_5_node, raise;

  Comparator comparator_1 (.a(intput_value), .b(8'h62), .eq(comparator_1_eq));  // open: gt, lt
  Pull_Resistor pull_resistor_1 (.node(pull_resistor_1_node));
  Comparator comparator_2 (.a(intput_value), .b(8'h61), .eq(comparator_2_eq));  // open: gt, lt
  Pull_Resistor pull_resistor_2 (.node(pull_resistor_2_node));
  Multiplexer #(.width(8)) multiplexer_1 (
    .in0(pull_resistor_1_node), .in1(8'h5), .out(bet), .sel(comparator_1_eq));  // open: en
  Multiplexer #(.width(8)) multiplexer_2 (
    .in0(pull_resistor_2_node), .in1(8'h2), .out(call), .sel(comparator_2_eq));  // open: en
  Comparator comparator_3 (.a(intput_value), .b(8'h69), .eq(comparator_3_eq));  // open: gt, lt
  Pull_Resistor pull_resistor_3 (.node(pull_resistor_3_node));
  Comparator comparator_4 (.a(intput_value), .b(8'h68), .eq(comparator_4_eq));  // open: gt, lt
  Pull_Resistor pull_resistor_4 (.node(pull_resistor_4_node));
  Multiplexer #(.width(8)) multiplexer_3 (
    .in0(pull_resistor_3_node), .in1(8'h3), .out(raise), .sel(comparator_3_eq));  // open: en
  Multiplexer #(.width(8)) multiplexer_4 (
    .in0(pull_resistor_4_node), .in1(8'h4), .out(check), .sel(comparator_4_eq));  // open: en
  Comparator comparator_5 (.a(intput_value), .b(8'h66), .eq(comparator_5_eq));  // open: gt, lt
  Pull_Resistor pull_resistor_5 (.node(pull_resistor_5_node));
  Multiplexer #(.width(8)) multiplexer_5 (
    .in0(pull_resistor_5_node), .in1(8'h1), .out(fold), .sel(comparator_5_eq));  // open: en
  assign or_1_out = bet | call | raise | check | fold;  // OR_Gate or_1, 8 bits wide
  Multiplexer #(.width(8)) multiplexer_6 (
    .in0(output_value[7:0]), .in1(or_1_out), .out(multiplexer_6_out), .sel(not_2_out));  // open: en
  Register register_1 (.D(multiplexer_6_out), .Q(output_value[7:0]), .clk(not_1_out));  // open: en, clr
  not not_1 (not_1_out, clock);
  not not_2 (not_2_out, comparator_6_eq);
  Comparator comparator_6 (.a(or_1_out), .b({8{1'b0}}), .eq(comparator_6_eq));  // open: gt, lt

  assign output_value[15:8] = {8{1'b0}};

  // Other names for the same wires on the sheet: input_value[7:0] = intput_value
endmodule

module Bid (
  input  in_1,
  input  in_2,
  input  [7:0] in_3,
  output [15:0] out_4
);

  wire and_1_out, comparator_1_gt, comparator_2_lt, not_1_out;
  wire [7:0] adder_1_out, multiplexer_1_out, multiplexer_2_out, multiplier_1_out, subtractor_1_out;

  Comparator comparator_1 (.a(in_3), .b(8'h29), .gt(comparator_1_gt));  // open: eq, lt
  Comparator comparator_2 (.a(in_3), .b(8'h40), .lt(comparator_2_lt));  // open: gt, eq
  and and_1 (and_1_out, comparator_1_gt, comparator_2_lt);
  Multiplexer #(.width(8)) multiplexer_1 (
    .in0({8{1'b0}}), .in1(subtractor_1_out), .out(multiplexer_1_out), .sel(and_1_out));  // open: en
  Subtractor subtractor_1 (.a(in_3), .b(8'h30), .out(subtractor_1_out));  // open: bin, bout
  Adder adder_1 (.a(multiplexer_2_out), .b(multiplexer_1_out), .out(adder_1_out));  // open: cin, cout
  not not_1 (not_1_out, in_2);
  Register register_1 (.D(adder_1_out), .Q(out_4[7:0]), .clk(not_1_out), .clr(in_1));  // open: en
  Multiplexer #(.width(8)) multiplexer_2 (
    .in0(out_4[7:0]), .in1(multiplier_1_out), .out(multiplexer_2_out), .sel(and_1_out));  // open: en
  Multiplier multiplier_1 (.a(out_4[7:0]), .b(8'ha), .out(multiplier_1_out));  // open: cin, cout

  assign out_4[15:8] = {8{1'b0}};

  // Other names for the same wires on the sheet: input_num[7:0] = in_3; output_num[7:0] = out_4[7:0]
endmodule

module Randome_numbers (
  input  in_1,
  output [5:0] out_2,
  output [5:0] out_3,
  output [5:0] out_4,
  output [5:0] in_memory,
  output [5:0] out_6,
  output [5:0] out_7,
  output [5:0] out_8,
  output [5:0] out_9,
  output [5:0] out_10,
  output [5:0] out_11,
  output [5:0] out_12,
  output [5:0] out_13,
  output [5:0] out_14,
  output [5:0] out_15,
  output [5:0] out_16,
  output [5:0] out_17,
  output [5:0] out_18,
  output [5:0] out_19,
  output [5:0] out_20,
  output [5:0] out_21,
  output [5:0] out_22,
  output [5:0] out_23,
  output [5:0] out_24,
  output [5:0] out_25,
  output [5:0] out_26,
  output [5:0] out_27,
  output [5:0] out_28,
  output [5:0] out_29,
  output [5:0] out_30,
  output [5:0] out_31,
  output [5:0] out_32
);

  wire comparator_1_eq, comparator_2_eq, comparator_3_eq, comparator_4_eq, comparator_5_eq, comparator_6_eq,
       comparator_7_eq, comparator_8_eq, comparator_9_eq, comparator_10_eq, comparator_11_eq,
       comparator_12_eq, comparator_13_eq, comparator_14_eq, comparator_15_eq, comparator_16_eq,
       comparator_17_eq, comparator_18_eq, comparator_19_eq, comparator_20_eq, comparator_21_eq,
       comparator_22_eq, comparator_23_eq, comparator_24_eq, comparator_25_eq, comparator_26_eq,
       comparator_27_eq, comparator_28_eq, comparator_29_eq, comparator_30_eq, comparator_31_eq,
       comparator_32_eq, comparator_33_eq, comparator_34_eq, comparator_35_eq, comparator_36_eq,
       comparator_37_eq, comparator_38_gt, comparator_39_eq, comparator_40_eq, comparator_41_eq,
       comparator_42_eq, comparator_43_eq, comparator_44_eq, comparator_45_eq, comparator_46_eq,
       comparator_47_eq, comparator_48_eq, comparator_49_eq, comparator_50_eq, comparator_51_eq,
       comparator_52_eq, comparator_53_eq, comparator_54_eq, comparator_55_eq, comparator_56_eq,
       comparator_57_eq, comparator_58_eq, comparator_59_eq, comparator_60_eq, comparator_61_eq, first_or,
       not_1_out, not_2_out, not_3_out, not_4_out, not_5_out, not_6_out, not_7_out, not_8_out, not_9_out,
       not_10_out, not_11_out, not_12_out, not_13_out, not_14_out, not_15_out, not_16_out, not_17_out,
       not_18_out, not_19_out, not_20_out, not_21_out, not_22_out, not_23_out, not_24_out, not_25_out,
       not_26_out, not_27_out, not_28_out, not_29_out, or_4_out, or_5_out, second_or, third_or;
  wire [5:0] multiplexer_1_out, multiplexer_2_out, multiplexer_3_out, multiplexer_4_out, multiplexer_5_out,
       multiplexer_6_out, multiplexer_7_out, multiplexer_8_out, multiplexer_9_out, multiplexer_10_out,
       multiplexer_11_out, multiplexer_12_out, multiplexer_13_out, multiplexer_14_out, multiplexer_15_out,
       multiplexer_17_out, multiplexer_18_out, multiplexer_19_out, multiplexer_20_out, multiplexer_21_out,
       multiplexer_22_out, multiplexer_23_out, multiplexer_24_out, multiplexer_25_out, multiplexer_26_out,
       multiplexer_27_out, multiplexer_28_out, multiplexer_29_out, multiplexer_30_out, multiplexer_31_out,
       multiplexer_32_out, multiplexer_33_out, multiplexer_34_out, multiplexer_35_out, multiplexer_36_out,
       multiplexer_37_out, multiplexer_38_out, multiplexer_39_out, multiplexer_40_out, multiplexer_41_out,
       multiplexer_42_out, multiplexer_43_out, multiplexer_44_out, multiplexer_45_out, multiplexer_46_out,
       multiplexer_47_out, multiplexer_48_out, multiplexer_49_out, multiplexer_50_out, multiplexer_51_out,
       multiplexer_52_out, multiplexer_53_out, multiplexer_54_out, multiplexer_55_out, multiplexer_56_out,
       multiplexer_57_out, multiplexer_58_out, multiplexer_59_out, multiplexer_60_out, random_num;

  Multiplexer #(.width(6)) multiplexer_1 (
    .in0(out_2), .in1(in_memory), .out(multiplexer_1_out), .sel(comparator_31_eq));  // open: en
  Comparator #(.width(6)) comparator_1 (.a(out_2), .b(random_num), .eq(comparator_1_eq));  // open: gt, lt
  Comparator #(.width(6)) comparator_2 (.a(out_3), .b(random_num), .eq(comparator_2_eq));  // open: gt, lt
  Comparator #(.width(6)) comparator_3 (.a(out_4), .b(random_num), .eq(comparator_3_eq));  // open: gt, lt
  Comparator #(.width(6)) comparator_4 (.a(out_6), .b(random_num), .eq(comparator_4_eq));  // open: gt, lt
  Comparator #(.width(6)) comparator_5 (.a(out_7), .b(random_num), .eq(comparator_5_eq));  // open: gt, lt
  Comparator #(.width(6)) comparator_6 (.a(out_8), .b(random_num), .eq(comparator_6_eq));  // open: gt, lt
  Comparator #(.width(6)) comparator_7 (.a(out_9), .b(random_num), .eq(comparator_7_eq));  // open: gt, lt
  Comparator #(.width(6)) comparator_8 (.a(out_10), .b(random_num), .eq(comparator_8_eq));  // open: gt, lt
  Comparator #(.width(6)) comparator_9 (.a(out_11), .b(random_num), .eq(comparator_9_eq));  // open: gt, lt
  Comparator #(.width(6)) comparator_10 (.a(out_12), .b(random_num), .eq(comparator_10_eq));  // open: gt, lt
  Comparator #(.width(6)) comparator_11 (.a(out_13), .b(random_num), .eq(comparator_11_eq));  // open: gt, lt
  Comparator #(.width(6)) comparator_12 (.a(out_14), .b(random_num), .eq(comparator_12_eq));  // open: gt, lt
  Comparator #(.width(6)) comparator_13 (.a(out_15), .b(random_num), .eq(comparator_13_eq));  // open: gt, lt
  Comparator #(.width(6)) comparator_14 (.a(out_16), .b(random_num), .eq(comparator_14_eq));  // open: gt, lt
  Comparator #(.width(6)) comparator_15 (.a(out_17), .b(random_num), .eq(comparator_15_eq));  // open: gt, lt
  Comparator #(.width(6)) comparator_16 (.a(out_18), .b(random_num), .eq(comparator_16_eq));  // open: gt, lt
  Comparator #(.width(6)) comparator_17 (.a(out_19), .b(random_num), .eq(comparator_17_eq));  // open: gt, lt
  Comparator #(.width(6)) comparator_18 (.a(out_20), .b(random_num), .eq(comparator_18_eq));  // open: gt, lt
  Comparator #(.width(6)) comparator_19 (.a(out_21), .b(random_num), .eq(comparator_19_eq));  // open: gt, lt
  Comparator #(.width(6)) comparator_20 (.a(out_22), .b(random_num), .eq(comparator_20_eq));  // open: gt, lt
  Comparator #(.width(6)) comparator_21 (.a(out_23), .b(random_num), .eq(comparator_21_eq));  // open: gt, lt
  Comparator #(.width(6)) comparator_22 (.a(out_24), .b(random_num), .eq(comparator_22_eq));  // open: gt, lt
  Comparator #(.width(6)) comparator_23 (.a(out_25), .b(random_num), .eq(comparator_23_eq));  // open: gt, lt
  Comparator #(.width(6)) comparator_24 (.a(out_26), .b(random_num), .eq(comparator_24_eq));  // open: gt, lt
  Comparator #(.width(6)) comparator_25 (.a(out_27), .b(random_num), .eq(comparator_25_eq));  // open: gt, lt
  Comparator #(.width(6)) comparator_26 (.a(out_28), .b(random_num), .eq(comparator_26_eq));  // open: gt, lt
  Comparator #(.width(6)) comparator_27 (.a(out_29), .b(random_num), .eq(comparator_27_eq));  // open: gt, lt
  Comparator #(.width(6)) comparator_28 (.a(out_30), .b(random_num), .eq(comparator_28_eq));  // open: gt, lt
  Comparator #(.width(6)) comparator_29 (.a(out_31), .b(random_num), .eq(comparator_29_eq));  // open: gt, lt
  Comparator #(.width(6)) comparator_30 (.a(out_32), .b(random_num), .eq(comparator_30_eq));  // open: gt, lt
  Register #(.width(6)) register_1 (.D(multiplexer_1_out), .Q(out_2), .clk(in_1));  // open: en, clr
  Comparator #(.width(6)) comparator_31 (.a(out_2), .b({6{1'b0}}), .eq(comparator_31_eq));  // open: gt, lt
  not not_1 (not_1_out, comparator_31_eq);
  Multiplexer #(.width(6)) multiplexer_2 (
    .in0(out_3), .in1(multiplexer_3_out), .out(multiplexer_2_out), .sel(not_1_out));  // open: en
  Multiplexer #(.width(6)) multiplexer_3 (
    .in0(out_3), .in1(in_memory), .out(multiplexer_3_out), .sel(comparator_32_eq));  // open: en
  Register #(.width(6)) register_2 (.D(multiplexer_2_out), .Q(out_3), .clk(in_1));  // open: en, clr
  Comparator #(.width(6)) comparator_32 (.a(out_3), .b({6{1'b0}}), .eq(comparator_32_eq));  // open: gt, lt
  not not_2 (not_2_out, comparator_32_eq);
  Multiplexer #(.width(6)) multiplexer_4 (
    .in0(out_4), .in1(in_memory), .out(multiplexer_4_out), .sel(comparator_33_eq));  // open: en
  or or_1 (first_or, comparator_1_eq, comparator_2_eq, comparator_3_eq, comparator_4_eq, comparator_5_eq, comparator_6_eq, comparator_7_eq, comparator_8_eq, comparator_9_eq, comparator_10_eq);
  or or_2 (second_or, comparator_11_eq, comparator_12_eq, comparator_13_eq, comparator_14_eq, comparator_15_eq, comparator_16_eq, comparator_17_eq, comparator_18_eq, comparator_19_eq, comparator_20_eq);
  or or_3 (third_or, comparator_21_eq, comparator_22_eq, comparator_23_eq, comparator_24_eq, comparator_25_eq, comparator_26_eq, comparator_27_eq, comparator_28_eq, comparator_29_eq, comparator_30_eq);
  Multiplexer #(.width(6)) multiplexer_5 (
    .in0(out_4), .in1(multiplexer_4_out), .out(multiplexer_5_out), .sel(not_2_out));  // open: en
  Register #(.width(6)) register_3 (.D(multiplexer_5_out), .Q(out_4), .clk(in_1));  // open: en, clr
  Comparator #(.width(6)) comparator_33 (.a(out_4), .b({6{1'b0}}), .eq(comparator_33_eq));  // open: gt, lt
  not not_3 (not_3_out, comparator_33_eq);
  Multiplexer #(.width(6)) multiplexer_6 (
    .in0(out_6), .in1(multiplexer_7_out), .out(multiplexer_6_out), .sel(not_3_out));  // open: en
  Multiplexer #(.width(6)) multiplexer_7 (
    .in0(out_6), .in1(in_memory), .out(multiplexer_7_out), .sel(comparator_34_eq));  // open: en
  Register #(.width(6)) register_4 (.D(multiplexer_6_out), .Q(out_6), .clk(in_1));  // open: en, clr
  Multiplexer #(.width(6)) multiplexer_8 (
    .in0(out_7), .in1(in_memory), .out(multiplexer_8_out), .sel(comparator_35_eq));  // open: en
  Comparator #(.width(6)) comparator_34 (.a(out_6), .b({6{1'b0}}), .eq(comparator_34_eq));  // open: gt, lt
  not not_4 (not_4_out, comparator_34_eq);
  Register #(.width(6)) register_5 (.D(multiplexer_9_out), .Q(out_7), .clk(in_1));  // open: en, clr
  Multiplexer #(.width(6)) multiplexer_9 (
    .in0(out_7), .in1(multiplexer_8_out), .out(multiplexer_9_out), .sel(not_4_out));  // open: en
  Comparator #(.width(6)) comparator_35 (.a(out_7), .b({6{1'b0}}), .eq(comparator_35_eq));  // open: gt, lt
  not not_5 (not_5_out, comparator_35_eq);
  Multiplexer #(.width(6)) multiplexer_10 (
    .in0(out_8), .in1(in_memory), .out(multiplexer_10_out), .sel(comparator_36_eq));  // open: en
  Multiplexer #(.width(6)) multiplexer_11 (
    .in0(out_8), .in1(multiplexer_10_out), .out(multiplexer_11_out), .sel(not_5_out));  // open: en
  Register #(.width(6)) register_6 (.D(multiplexer_11_out), .Q(out_8), .clk(in_1));  // open: en, clr
  Random #(.width(6)) random_1 (.clk(in_1), .out(random_num));  // open: next, clr
  Comparator #(.width(6)) comparator_36 (.a(out_8), .b({6{1'b0}}), .eq(comparator_36_eq));  // open: gt, lt
  not not_6 (not_6_out, comparator_36_eq);
  Multiplexer #(.width(6)) multiplexer_12 (
    .in0(out_9), .in1(multiplexer_13_out), .out(multiplexer_12_out), .sel(not_6_out));  // open: en
  Multiplexer #(.width(6)) multiplexer_13 (
    .in0(out_9), .in1(in_memory), .out(multiplexer_13_out), .sel(comparator_37_eq));  // open: en
  Register #(.width(6)) register_7 (.D(multiplexer_12_out), .Q(out_9), .clk(in_1));  // open: en, clr
  Comparator #(.width(6)) comparator_37 (.a(out_9), .b({6{1'b0}}), .eq(comparator_37_eq));  // open: gt, lt
  Multiplexer #(.width(6)) multiplexer_14 (
    .in0(out_10), .in1(in_memory), .out(multiplexer_14_out), .sel(comparator_39_eq));  // open: en
  or or_4 (or_4_out, first_or, second_or, third_or);
  Comparator #(.width(6), .mode("unsigned")) comparator_38 (
    .a(random_num), .b(6'b110100), .gt(comparator_38_gt));  // open: eq, lt
  not not_7 (not_7_out, comparator_37_eq);
  Multiplexer #(.width(6)) multiplexer_15 (
    .in0(out_10), .in1(multiplexer_14_out), .out(multiplexer_15_out), .sel(not_7_out));  // open: en
  Register #(.width(6)) register_8 (.D(multiplexer_15_out), .Q(out_10), .clk(in_1));  // open: en, clr
  Multiplexer #(.width(6)) multiplexer_16 (
    .in0(random_num), .in1({6{1'b0}}), .out(in_memory), .sel(or_5_out));  // open: en
  or or_5 (or_5_out, or_4_out, comparator_38_gt);
  Comparator #(.width(6)) comparator_39 (.a(out_10), .b({6{1'b0}}), .eq(comparator_39_eq));  // open: gt, lt
  not not_8 (not_8_out, comparator_39_eq);
  Multiplexer #(.width(6)) multiplexer_17 (
    .in0(out_11), .in1(multiplexer_18_out), .out(multiplexer_17_out), .sel(not_8_out));  // open: en
  Multiplexer #(.width(6)) multiplexer_18 (
    .in0(out_11), .in1(in_memory), .out(multiplexer_18_out), .sel(comparator_40_eq));  // open: en
  Pull_Resistor pull_resistor_1 (.node(in_memory));
  Register #(.width(6)) register_9 (.D(multiplexer_17_out), .Q(out_11), .clk(in_1));  // open: en, clr
  Comparator #(.width(6)) comparator_40 (.a(out_11), .b({6{1'b0}}), .eq(comparator_40_eq));  // open: gt, lt
  not not_9 (not_9_out, comparator_40_eq);
  Multiplexer #(.width(6)) multiplexer_19 (
    .in0(out_12), .in1(multiplexer_20_out), .out(multiplexer_19_out), .sel(not_9_out));  // open: en
  Multiplexer #(.width(6)) multiplexer_20 (
    .in0(out_12), .in1(in_memory), .out(multiplexer_20_out), .sel(comparator_41_eq));  // open: en
  Register #(.width(6)) register_10 (.D(multiplexer_19_out), .Q(out_12), .clk(in_1));  // open: en, clr
  Comparator #(.width(6)) comparator_41 (.a(out_12), .b({6{1'b0}}), .eq(comparator_41_eq));  // open: gt, lt
  not not_10 (not_10_out, comparator_41_eq);
  Multiplexer #(.width(6)) multiplexer_21 (
    .in0(out_13), .in1(in_memory), .out(multiplexer_21_out), .sel(comparator_42_eq));  // open: en
  Multiplexer #(.width(6)) multiplexer_22 (
    .in0(out_13), .in1(multiplexer_21_out), .out(multiplexer_22_out), .sel(not_10_out));  // open: en
  Register #(.width(6)) register_11 (.D(multiplexer_22_out), .Q(out_13), .clk(in_1));  // open: en, clr
  Comparator #(.width(6)) comparator_42 (.a(out_13), .b({6{1'b0}}), .eq(comparator_42_eq));  // open: gt, lt
  not not_11 (not_11_out, comparator_42_eq);
  Multiplexer #(.width(6)) multiplexer_23 (
    .in0(out_14), .in1(multiplexer_24_out), .out(multiplexer_23_out), .sel(not_11_out));  // open: en
  Multiplexer #(.width(6)) multiplexer_24 (
    .in0(out_14), .in1(in_memory), .out(multiplexer_24_out), .sel(comparator_43_eq));  // open: en
  Register #(.width(6)) register_12 (.D(multiplexer_23_out), .Q(out_14), .clk(in_1));  // open: en, clr
  Multiplexer #(.width(6)) multiplexer_25 (
    .in0(out_15), .in1(in_memory), .out(multiplexer_25_out), .sel(comparator_44_eq));  // open: en
  Comparator #(.width(6)) comparator_43 (.a(out_14), .b({6{1'b0}}), .eq(comparator_43_eq));  // open: gt, lt
  not not_12 (not_12_out, comparator_43_eq);
  Multiplexer #(.width(6)) multiplexer_26 (
    .in0(out_15), .in1(multiplexer_25_out), .out(multiplexer_26_out), .sel(not_12_out));  // open: en
  Register #(.width(6)) register_13 (.D(multiplexer_26_out), .Q(out_15), .clk(in_1));  // open: en, clr
  Comparator #(.width(6)) comparator_44 (.a(out_15), .b({6{1'b0}}), .eq(comparator_44_eq));  // open: gt, lt
  not not_13 (not_13_out, comparator_44_eq);
  Multiplexer #(.width(6)) multiplexer_27 (
    .in0(out_16), .in1(in_memory), .out(multiplexer_27_out), .sel(comparator_45_eq));  // open: en
  Register #(.width(6)) register_14 (.D(multiplexer_28_out), .Q(out_16), .clk(in_1));  // open: en, clr
  Multiplexer #(.width(6)) multiplexer_28 (
    .in0(out_16), .in1(multiplexer_27_out), .out(multiplexer_28_out), .sel(not_13_out));  // open: en
  Comparator #(.width(6)) comparator_45 (.a(out_16), .b({6{1'b0}}), .eq(comparator_45_eq));  // open: gt, lt
  not not_14 (not_14_out, comparator_45_eq);
  Multiplexer #(.width(6)) multiplexer_29 (
    .in0(out_17), .in1(multiplexer_30_out), .out(multiplexer_29_out), .sel(not_14_out));  // open: en
  Multiplexer #(.width(6)) multiplexer_30 (
    .in0(out_17), .in1(in_memory), .out(multiplexer_30_out), .sel(comparator_46_eq));  // open: en
  Register #(.width(6)) register_15 (.D(multiplexer_29_out), .Q(out_17), .clk(in_1));  // open: en, clr
  Comparator #(.width(6)) comparator_46 (.a(out_17), .b({6{1'b0}}), .eq(comparator_46_eq));  // open: gt, lt
  Multiplexer #(.width(6)) multiplexer_31 (
    .in0(out_18), .in1(in_memory), .out(multiplexer_31_out), .sel(comparator_47_eq));  // open: en
  not not_15 (not_15_out, comparator_46_eq);
  Register #(.width(6)) register_16 (.D(multiplexer_32_out), .Q(out_18), .clk(in_1));  // open: en, clr
  Multiplexer #(.width(6)) multiplexer_32 (
    .in0(out_18), .in1(multiplexer_31_out), .out(multiplexer_32_out), .sel(not_15_out));  // open: en
  Comparator #(.width(6)) comparator_47 (.a(out_18), .b({6{1'b0}}), .eq(comparator_47_eq));  // open: gt, lt
  not not_16 (not_16_out, comparator_47_eq);
  Multiplexer #(.width(6)) multiplexer_33 (
    .in0(out_19), .in1(multiplexer_34_out), .out(multiplexer_33_out), .sel(not_16_out));  // open: en
  Multiplexer #(.width(6)) multiplexer_34 (
    .in0(out_19), .in1(in_memory), .out(multiplexer_34_out), .sel(comparator_48_eq));  // open: en
  Register #(.width(6)) register_17 (.D(multiplexer_33_out), .Q(out_19), .clk(in_1));  // open: en, clr
  Comparator #(.width(6)) comparator_48 (.a(out_19), .b({6{1'b0}}), .eq(comparator_48_eq));  // open: gt, lt
  not not_17 (not_17_out, comparator_48_eq);
  Multiplexer #(.width(6)) multiplexer_35 (
    .in0(out_20), .in1(multiplexer_36_out), .out(multiplexer_35_out), .sel(not_17_out));  // open: en
  Multiplexer #(.width(6)) multiplexer_36 (
    .in0(out_20), .in1(in_memory), .out(multiplexer_36_out), .sel(comparator_49_eq));  // open: en
  Register #(.width(6)) register_18 (.D(multiplexer_35_out), .Q(out_20), .clk(in_1));  // open: en, clr
  Comparator #(.width(6)) comparator_49 (.a(out_20), .b({6{1'b0}}), .eq(comparator_49_eq));  // open: gt, lt
  not not_18 (not_18_out, comparator_49_eq);
  Multiplexer #(.width(6)) multiplexer_37 (
    .in0(out_21), .in1(in_memory), .out(multiplexer_37_out), .sel(comparator_50_eq));  // open: en
  Register #(.width(6)) register_19 (.D(multiplexer_38_out), .Q(out_21), .clk(in_1));  // open: en, clr
  Multiplexer #(.width(6)) multiplexer_38 (
    .in0(out_21), .in1(multiplexer_37_out), .out(multiplexer_38_out), .sel(not_18_out));  // open: en
  Comparator #(.width(6)) comparator_50 (.a(out_21), .b({6{1'b0}}), .eq(comparator_50_eq));  // open: gt, lt
  not not_19 (not_19_out, comparator_50_eq);
  Multiplexer #(.width(6)) multiplexer_39 (
    .in0(out_22), .in1(multiplexer_40_out), .out(multiplexer_39_out), .sel(not_19_out));  // open: en
  Multiplexer #(.width(6)) multiplexer_40 (
    .in0(out_22), .in1(in_memory), .out(multiplexer_40_out), .sel(comparator_51_eq));  // open: en
  Register #(.width(6)) register_20 (.D(multiplexer_39_out), .Q(out_22), .clk(in_1));  // open: en, clr
  Multiplexer #(.width(6)) multiplexer_41 (
    .in0(out_23), .in1(in_memory), .out(multiplexer_41_out), .sel(comparator_52_eq));  // open: en
  Comparator #(.width(6)) comparator_51 (.a(out_22), .b({6{1'b0}}), .eq(comparator_51_eq));  // open: gt, lt
  not not_20 (not_20_out, comparator_51_eq);
  Multiplexer #(.width(6)) multiplexer_42 (
    .in0(out_23), .in1(multiplexer_41_out), .out(multiplexer_42_out), .sel(not_20_out));  // open: en
  Register #(.width(6)) register_21 (.D(multiplexer_42_out), .Q(out_23), .clk(in_1));  // open: en, clr
  Comparator #(.width(6)) comparator_52 (.a(out_23), .b({6{1'b0}}), .eq(comparator_52_eq));  // open: gt, lt
  not not_21 (not_21_out, comparator_52_eq);
  Multiplexer #(.width(6)) multiplexer_43 (
    .in0(out_24), .in1(in_memory), .out(multiplexer_43_out), .sel(comparator_53_eq));  // open: en
  Multiplexer #(.width(6)) multiplexer_44 (
    .in0(out_24), .in1(multiplexer_43_out), .out(multiplexer_44_out), .sel(not_21_out));  // open: en
  Register #(.width(6)) register_22 (.D(multiplexer_44_out), .Q(out_24), .clk(in_1));  // open: en, clr
  Comparator #(.width(6)) comparator_53 (.a(out_24), .b({6{1'b0}}), .eq(comparator_53_eq));  // open: gt, lt
  not not_22 (not_22_out, comparator_53_eq);
  Multiplexer #(.width(6)) multiplexer_45 (
    .in0(out_25), .in1(multiplexer_46_out), .out(multiplexer_45_out), .sel(not_22_out));  // open: en
  Multiplexer #(.width(6)) multiplexer_46 (
    .in0(out_25), .in1(in_memory), .out(multiplexer_46_out), .sel(comparator_54_eq));  // open: en
  Register #(.width(6)) register_23 (.D(multiplexer_45_out), .Q(out_25), .clk(in_1));  // open: en, clr
  Comparator #(.width(6)) comparator_54 (.a(out_25), .b({6{1'b0}}), .eq(comparator_54_eq));  // open: gt, lt
  Multiplexer #(.width(6)) multiplexer_47 (
    .in0(out_26), .in1(in_memory), .out(multiplexer_47_out), .sel(comparator_55_eq));  // open: en
  not not_23 (not_23_out, comparator_54_eq);
  Register #(.width(6)) register_24 (.D(multiplexer_48_out), .Q(out_26), .clk(in_1));  // open: en, clr
  Multiplexer #(.width(6)) multiplexer_48 (
    .in0(out_26), .in1(multiplexer_47_out), .out(multiplexer_48_out), .sel(not_23_out));  // open: en
  Comparator #(.width(6)) comparator_55 (.a(out_26), .b({6{1'b0}}), .eq(comparator_55_eq));  // open: gt, lt
  not not_24 (not_24_out, comparator_55_eq);
  Multiplexer #(.width(6)) multiplexer_49 (
    .in0(out_27), .in1(multiplexer_50_out), .out(multiplexer_49_out), .sel(not_24_out));  // open: en
  Multiplexer #(.width(6)) multiplexer_50 (
    .in0(out_27), .in1(in_memory), .out(multiplexer_50_out), .sel(comparator_56_eq));  // open: en
  Register #(.width(6)) register_25 (.D(multiplexer_49_out), .Q(out_27), .clk(in_1));  // open: en, clr
  Comparator #(.width(6)) comparator_56 (.a(out_27), .b({6{1'b0}}), .eq(comparator_56_eq));  // open: gt, lt
  not not_25 (not_25_out, comparator_56_eq);
  Multiplexer #(.width(6)) multiplexer_51 (
    .in0(out_28), .in1(multiplexer_52_out), .out(multiplexer_51_out), .sel(not_25_out));  // open: en
  Multiplexer #(.width(6)) multiplexer_52 (
    .in0(out_28), .in1(in_memory), .out(multiplexer_52_out), .sel(comparator_57_eq));  // open: en
  Register #(.width(6)) register_26 (.D(multiplexer_51_out), .Q(out_28), .clk(in_1));  // open: en, clr
  Comparator #(.width(6)) comparator_57 (.a(out_28), .b({6{1'b0}}), .eq(comparator_57_eq));  // open: gt, lt
  not not_26 (not_26_out, comparator_57_eq);
  Multiplexer #(.width(6)) multiplexer_53 (
    .in0(out_29), .in1(in_memory), .out(multiplexer_53_out), .sel(comparator_58_eq));  // open: en
  Multiplexer #(.width(6)) multiplexer_54 (
    .in0(out_29), .in1(multiplexer_53_out), .out(multiplexer_54_out), .sel(not_26_out));  // open: en
  Register #(.width(6)) register_27 (.D(multiplexer_54_out), .Q(out_29), .clk(in_1));  // open: en, clr
  Comparator #(.width(6)) comparator_58 (.a(out_29), .b({6{1'b0}}), .eq(comparator_58_eq));  // open: gt, lt
  not not_27 (not_27_out, comparator_58_eq);
  Multiplexer #(.width(6)) multiplexer_55 (
    .in0(out_30), .in1(multiplexer_56_out), .out(multiplexer_55_out), .sel(not_27_out));  // open: en
  Multiplexer #(.width(6)) multiplexer_56 (
    .in0(out_30), .in1(in_memory), .out(multiplexer_56_out), .sel(comparator_59_eq));  // open: en
  Register #(.width(6)) register_28 (.D(multiplexer_55_out), .Q(out_30), .clk(in_1));  // open: en, clr
  Multiplexer #(.width(6)) multiplexer_57 (
    .in0(out_31), .in1(in_memory), .out(multiplexer_57_out), .sel(comparator_60_eq));  // open: en
  Comparator #(.width(6)) comparator_59 (.a(out_30), .b({6{1'b0}}), .eq(comparator_59_eq));  // open: gt, lt
  not not_28 (not_28_out, comparator_59_eq);
  Multiplexer #(.width(6)) multiplexer_58 (
    .in0(out_31), .in1(multiplexer_57_out), .out(multiplexer_58_out), .sel(not_28_out));  // open: en
  Register #(.width(6)) register_29 (.D(multiplexer_58_out), .Q(out_31), .clk(in_1));  // open: en, clr
  Comparator #(.width(6)) comparator_60 (.a(out_31), .b({6{1'b0}}), .eq(comparator_60_eq));  // open: gt, lt
  not not_29 (not_29_out, comparator_60_eq);
  Multiplexer #(.width(6)) multiplexer_59 (
    .in0(out_32), .in1(in_memory), .out(multiplexer_59_out), .sel(comparator_61_eq));  // open: en
  Register #(.width(6)) register_30 (.D(multiplexer_60_out), .Q(out_32), .clk(in_1));  // open: en, clr
  Multiplexer #(.width(6)) multiplexer_60 (
    .in0(out_32), .in1(multiplexer_59_out), .out(multiplexer_60_out), .sel(not_29_out));  // open: en
  Comparator #(.width(6)) comparator_61 (.a(out_32), .b({6{1'b0}}), .eq(comparator_61_eq));  // open: gt, lt

  // Other names for the same wires on the sheet: _1r[5:0] = out_2; _2r[5:0] = out_3; _3r[5:0] = out_4;
  //   _4r[5:0] = out_6; _5r[5:0] = out_7; _6r[5:0] = out_8; _7r[5:0] = out_9; _8r[5:0] = out_10; _9r[5:0] = out_11;
  //   _10r[5:0] = out_12; _11r[5:0] = out_13; _12r[5:0] = out_14; _13r[5:0] = out_15; _14r[5:0] = out_16;
  //   _15r[5:0] = out_17; _16r[5:0] = out_18; _17r[5:0] = out_19; _18r[5:0] = out_20; _19r[5:0] = out_21;
  //   _20r[5:0] = out_22; _21r[5:0] = out_23; _22r[5:0] = out_24; _23r[5:0] = out_25; _24r[5:0] = out_26;
  //   _25r[5:0] = out_27; _26r[5:0] = out_28; _27r[5:0] = out_29; _28r[5:0] = out_30; _29r[5:0] = out_31;
  //   _30r[5:0] = out_32; cclock = in_1; check_random_num[5:0] = in_memory
endmodule

module Random_store (
  input  [5:0] in_memory,
  input  [15:0] random_address,
  input  clk,
  output \break ,
  output [15:0] data_bus,
  output block,
  output [15:0] address_bus
);

  wire comparator_2_eq, comparator_3_eq, not_1_out;
  wire [15:0] adder_1_out, adder_2_out, multiplexer_1_out, multiplexer_2_out, multiplexer_3_out,
       register_1_q, subtractor_1_out;

  Adder #(.width(16)) adder_1 (.a(random_address), .b(16'h3c), .out(adder_1_out));  // open: cin, cout
  Adder #(.width(16)) adder_2 (.a(register_1_q), .b(16'h2), .out(adder_2_out));  // open: cin, cout
  Comparator #(.width(16), .mode("unsigned")) comparator_1 (
    .a(adder_1_out), .b(register_1_q), .gt(block));  // open: eq, lt
  Multiplexer #(.width(16)) multiplexer_1 (
    .in0(register_1_q), .in1(adder_2_out), .out(multiplexer_1_out), .sel(not_1_out));  // open: en
  not not_1 (not_1_out, comparator_2_eq);
  Comparator #(.width(6), .mode("unsigned")) comparator_2 (
    .a(in_memory), .b({6{1'b0}}), .eq(comparator_2_eq));  // open: gt, lt
  Transistor #(.\type ("n")) transistor_1 (.in(block), .out(\break ), .gate(block));
  Subtractor #(.width(16)) subtractor_1 (
    .a({{10{1'b0}}, in_memory}), .b(16'h1), .out(subtractor_1_out));  // open: bin, bout
  Comparator #(.width(16), .mode("unsigned")) comparator_3 (
    .a(register_1_q), .b({16{1'b0}}), .eq(comparator_3_eq));  // open: gt, lt
  Multiplexer #(.width(16)) multiplexer_2 (
    .in0(multiplexer_1_out), .in1(random_address), .out(multiplexer_2_out), .sel(comparator_3_eq));  // open: en
  Transistor #(.\type ("n"), .width(16)) transistor_2 (.in(subtractor_1_out), .out(data_bus), .gate(block));
  Multiplexer #(.width(16)) multiplexer_3 (
    .in0(register_1_q), .in1(multiplexer_2_out), .out(multiplexer_3_out), .sel(block));  // open: en
  Register #(.width(16)) register_1 (.D(multiplexer_3_out), .Q(register_1_q), .clk(clk));  // open: en, clr
  Transistor #(.\type ("n"), .width(16)) transistor_3 (.in(register_1_q), .out(address_bus), .gate(block));
endmodule

module Display_template (
  input  [7:0] in_1,
  input  in_2
);

  wire comparator_1_eq;
  wire [7:0] undriven;
  wire [15:0] adder_1_out, multiplexer_1_out, register_1_q;

  Adder #(.width(16)) adder_1 (.a(register_1_q), .b(16'h1), .out(adder_1_out));  // open: cin, cout
  Comparator #(.width(16)) comparator_1 (.a(16'h7bc), .b(register_1_q), .eq(comparator_1_eq));  // open: gt, lt
  // Probe on multiplexer_1_out
  Multiplexer #(.width(16)) multiplexer_1 (
    .in0(adder_1_out), .in1(register_1_q), .out(multiplexer_1_out), .sel(comparator_1_eq));  // open: en
  Register #(.width(16)) register_1 (.D(multiplexer_1_out), .Q(register_1_q), .clk(in_2));  // open: en, clr
  // ROM rom_1: pin names not known; wires that end beside it: register_1_q, 1'b1
  // Probe on in_1
  Transistor #(.width(8)) transistor_1 (.in(undriven), .out(in_1), .gate(comparator_1_eq));
endmodule
