// Logisim project renormal_name.circ as structural Verilog: 15 circuits, main circuit main
// C:\Ass_project\poker\out.img
module main (
  output out_1,
  output out_2
);

  wire block, \break , clk, clock, comparator_1_eq, comparator_2_eq, comparator_3_eq, comparator_3_gt,
       comparator_3_lt, comparator_4_eq, comparator_5_eq, comparator_6_eq, comparator_7_eq, comparator_8_eq,
       comparator_9_eq, comparator_10_eq, comparator_11_eq, comparator_12_eq, comparator_13_eq,
       comparator_14_eq, from_break, from_signal, mem, multiplexer_1_out, multiplexer_6_out,
       multiplexer_7_out, not_1_out, or_1_out, pull_resistor_10_node, read, register_1_q, sp_break,
       sp_break_1, sp_break_2, sp_break_3, sp_break_4, sp_clock, start, tag_1, tag_2, tag_3, tag_4, telnet,
       transistor_8_out, transistor_13_out, undriven, word, wr_rd;
  wire [7:0] ext_data, ext_data_1, ext_data_2, ext_data_3, ext_data_4, print_num_1_address,
       print_num_2_address, print_num_3_address, print_num_3_out_11, print_num_4_address, rom_1_data,
       rom_2_data, rom_3_data, rom_4_data, vec_adr;
  wire [15:0] adder_1_out, adder_2_out, address_bus, cdm_bar_1_p1, cdm_bar_1_p2, command,
       controlled_buffer_1_out, data_bus, from, how_much, multiplexer_3_out, multiplexer_4_out,
       multiplexer_5_out, multiplexer_8_out, multiplexer_9_out, multiplexer_10_out, multiplexer_11_out,
       multiplexer_12_out, multiplexer_13_out, multiplexer_14_out, multiplexer_16_out, multiplexer_17_out,
       multiplexer_18_out, multiplexer_19_out, multiplexer_20_out, multiplexer_21_out, multiplexer_22_out,
       multiplexer_23_out, multiplexer_24_out, num, print_num_3_out_12, pull_resistor_5_node, register_3_q,
       register_7_q, register_8_q, register_9_q, register_10_q, register_11_q, register_12_q, temporary_data,
       transistor_11_out, transistor_12_out;
  wire [15:8] transistor_10_out;

  Register #(.width(1)) register_1 (.D(1'b1), .Q(register_1_q), .clk(clk));  // open: en, clr
  Pull_Resistor pull_resistor_1 (.node(from_signal));
  Pull_Resistor pull_resistor_2 (.node(ext_data));
  Pull_Resistor pull_resistor_3 (.node(telnet));
  Pull_Resistor pull_resistor_4 (.node(clock));
  Transistor #(.\type ("n")) transistor_1 (.in(clk), .out(clock), .gate(start));
  Register #(.width(1)) register_2 (.D(register_1_q), .Q(start), .clk(clk));  // open: en, clr
  Clock clock_1 (.out(clk));
  Bid bid_1 (.in_2(vec_adr), .out_3(num), .in_1(clock));
  Commands commands_1 (.intput_value(vec_adr), .output_value(command), .clock(clock));
  Pull_Resistor pull_resistor_5 (.node(pull_resistor_5_node));
  Transistor #(.\type ("n"), .width(16)) transistor_2 (
    .in(register_3_q), .out(pull_resistor_5_node), .gate(from_break));
  Adder #(.width(16)) adder_1 (.a(pull_resistor_5_node), .b(16'h2), .out(adder_1_out));  // open: cin, cout
  Comparator #(.width(16)) comparator_1 (.a(address_bus), .b(16'hfc1a), .eq(comparator_1_eq));  // open: gt, lt
  Multiplexer multiplexer_1 (
    .in0(multiplexer_6_out), .in1(1'b0), .out(multiplexer_1_out), .sel(sp_break_2));  // open: en
  Multiplexer multiplexer_2 (.in0(multiplexer_1_out), .in1(1'b0), .out(sp_clock), .sel(sp_break_1));  // open: en
  // CdM_16 cdm_16_1: pin names not known; wires that end beside it: 1'b0, 1'b0
  Pull_Resistor pull_resistor_6 ();  // open: node
  Adder #(.width(16)) adder_2 (.a(from), .b(how_much), .out(adder_2_out));  // open: cin, cout
  Register #(.width(16)) register_3 (.D(multiplexer_3_out), .Q(register_3_q), .clk(clock));  // open: en, clr
  Multiplexer #(.width(16)) multiplexer_3 (
    .in0(from), .in1(adder_1_out), .out(multiplexer_3_out), .sel(from_signal));  // open: en
  Multiplexer #(.width(16)) multiplexer_4 (
    .in0(from), .in1(multiplexer_5_out), .out(multiplexer_4_out), .sel(comparator_1_eq));  // open: en
  Multiplexer #(.width(16)) multiplexer_5 (
    .in0({16{1'b0}}), .in1(data_bus), .out(multiplexer_5_out), .sel(comparator_1_eq));  // open: en
  Multiplexer multiplexer_6 (
    .in0(multiplexer_7_out), .in1(1'b0), .out(multiplexer_6_out), .sel(sp_break_4));  // open: en
  cdm_power cdm_power_1 (.from_signal(from_signal), .\break (\break ), .clock(clock));  // open: out_4
  Comparator comparator_2 (.a(vec_adr), .b(8'hd), .eq(comparator_2_eq));  // open: gt, lt
  Comparator #(.width(16), .mode("unsigned")) comparator_3 (
    .a(adder_2_out), .b(register_3_q), .gt(comparator_3_gt), .eq(comparator_3_eq), .lt(comparator_3_lt));
  or or_1 (or_1_out, comparator_3_eq, comparator_3_lt);
  Transistor #(.\type ("n"), .width(16)) transistor_3 (.in(register_3_q), .out(address_bus), .gate(from_break));
  Register #(.width(16)) register_4 (.D(multiplexer_4_out), .Q(from), .clk(clock));  // open: en, clr
  Multiplexer multiplexer_7 (.in0(undriven), .in1(1'b0), .out(multiplexer_7_out), .sel(sp_break_3));  // open: en
  Transistor #(.\type ("n")) transistor_4 (.in(1'b1), .out(sp_break), .gate(sp_break_1));
  Transistor #(.\type ("n")) transistor_5 (.in(1'b1), .out(sp_break), .gate(sp_break_2));
  Transistor #(.\type ("n")) transistor_6 (.in(1'b1), .out(sp_break), .gate(sp_break_3));
  Pull_Resistor pull_resistor_7 (.node(sp_break));
  Transistor #(.\type ("n")) transistor_7 (.in(1'b1), .out(sp_break), .gate(sp_break_4));
  // cdm_bar cdm_bar_1: pin names not known; wires that end beside it: cdm_bar_1_p1, cdm_bar_1_p2, mem, read, word, address_bus, \break 
  Multiplexer #(.width(16)) multiplexer_8 (
    .in0(command), .in1(num), .out(multiplexer_8_out), .sel(comparator_2_eq));  // open: en
  Multiplexer #(.width(16)) multiplexer_9 (
    .in0(16'hfc08), .in1(16'hfc0a), .out(multiplexer_9_out), .sel(comparator_2_eq));  // open: en
  and and_1 (from_break, from_signal, comparator_3_gt);
  // Probe on data_bus
  assign controlled_buffer_1_out = not_1_out ? cdm_bar_1_p1 : 16'bz;  // Controlled_Buffer controlled_buffer_1
  not not_1 (not_1_out, read);
  assign cdm_bar_1_p2 = read ? multiplexer_12_out : 16'bz;  // Controlled_Buffer controlled_buffer_2
  Multiplexer #(.width(16)) multiplexer_10 (
    .in0(multiplexer_8_out), .in1({16{1'b0}}), .out(multiplexer_10_out), .sel(comparator_4_eq));  // open: en
  Comparator comparator_4 (.a(vec_adr), .b(8'ha), .eq(comparator_4_eq));  // open: gt, lt
  Multiplexer #(.width(16)) multiplexer_11 (
    .in0(multiplexer_9_out), .in1(16'hfc00), .out(multiplexer_11_out), .sel(comparator_4_eq));  // open: en
  Transistor #(.\type ("n"), .gate("br")) transistor_8 (.in(or_1_out), .out(transistor_8_out), .gate(from_signal));
  Pull_Resistor pull_resistor_8 (.node(transistor_8_out));
  Transistor #(.\type ("n")) transistor_9 (.in(from_signal), .out(\break ), .gate(from_signal));
  Transistor #(.\type ("n"), .width(16)) transistor_10 (
    .in(data_bus), .out({transistor_10_out, ext_data}), .gate(from_break));
  Comparator comparator_5 (.a(vec_adr), .b({8{1'b0}}), .eq(comparator_5_eq));  // open: gt, lt
  // Probe on data_bus
  Multiplexer #(.width(16)) multiplexer_12 (.in0(data_bus), .out(multiplexer_12_out), .sel(\break ));  // open: in1, en
  Transistor #(.width(16)) transistor_11 (.in(multiplexer_13_out), .out(transistor_11_out), .gate(block));
  Multiplexer #(.width(16)) multiplexer_13 (
    .in1(multiplexer_10_out), .out(multiplexer_13_out), .sel(\break ));  // open: in0, en
  Multiplexer #(.width(16)) multiplexer_14 (
    .in1(multiplexer_11_out), .out(multiplexer_14_out), .sel(\break ));  // open: in0, en
  Transistor #(.gate("br"), .width(16)) transistor_12 (.in(multiplexer_14_out), .out(transistor_12_out), .gate(block));
  Transistor transistor_13 (.in(transistor_8_out), .out(transistor_13_out), .gate(block));
  Pull_Resistor pull_resistor_9 (.node(transistor_13_out));
  Transistor #(.\type ("n"), .width(16)) transistor_14 (.in(16'hfc1c), .out(address_bus), .gate(transistor_13_out));
  Pull_Resistor pull_resistor_10 (.node(pull_resistor_10_node));
  Transistor transistor_15 (.in(comparator_5_eq), .out(pull_resistor_10_node), .gate(block));
  Transistor #(.\type ("n")) transistor_16 (.in(1'b1), .out(telnet), .gate(pull_resistor_10_node));
  print_num print_num_1 (
    ._1_num(8'h28), ._2_num(8'h2f), ._3_num(8'h36), ._4_num(8'h3d), .data_bus(data_bus),
    .address_bus(address_bus), .clock(clock), .exit_data(ext_data_3), .address(print_num_1_address),
    .sp_break(sp_break_3), .tag_1(tag_3), .break_point(8'h3e), .start_add(16'hfc86));  // open: out_11, out_12
  // Probe on address_bus
  print_num print_num_2 (
    ._1_num(8'h28), ._2_num(8'h2f), ._3_num(8'h36), ._4_num(8'h3d), .data_bus(data_bus),
    .address_bus(address_bus), .clock(clock), .exit_data(ext_data_2), .address(print_num_2_address),
    .sp_break(sp_break_2), .tag_1(tag_2), .break_point(8'h3e), .start_add(16'hfc82));  // open: out_11, out_12
  // Probe on print_num_3_out_12
  // Probe on print_num_3_out_11
  Multiplexer #(.width(16)) multiplexer_15 (
    .in0(controlled_buffer_1_out), .in1(temporary_data), .out(data_bus), .sel(\break ));  // open: en
  Transistor #(.gate("br"), .width(16)) transistor_17 (.in(transistor_11_out), .out(data_bus), .gate(from_signal));
  Transistor #(.width(16)) transistor_18 (.in(transistor_12_out), .out(address_bus), .gate(from_signal));
  Transistor #(.\type ("n"), .gate("br"), .width(16)) transistor_19 (
    .in({16{1'b0}}), .out(data_bus), .gate(transistor_13_out));
  Comparator #(.width(16)) comparator_6 (.a(address_bus), .b(16'hfc1c), .eq(comparator_6_eq));  // open: gt, lt
  print_num print_num_3 (
    ._1_num(8'h23), ._2_num(8'h28), ._3_num(8'h2d), ._4_num(8'h32), .data_bus(data_bus),
    .address_bus(address_bus), .clock(clock), .exit_data(ext_data_1), .address(print_num_3_address),
    .sp_break(sp_break_1), .tag_1(tag_1), .break_point(8'h37), .start_add(16'hfc80),
    .out_11(print_num_3_out_11), .out_12(print_num_3_out_12));
  Transistor #(.\type ("n")) transistor_20 (.in(1'b1), .out(telnet), .gate(transistor_13_out));
  Multiplexer #(.width(16)) multiplexer_16 (
    .in0(how_much), .in1(multiplexer_17_out), .out(multiplexer_16_out), .sel(comparator_6_eq));  // open: en
  Multiplexer #(.width(16)) multiplexer_17 (
    .in0({16{1'b0}}), .in1(data_bus), .out(multiplexer_17_out), .sel(comparator_6_eq));  // open: en
  \interface  interface_1 (.exit_data(ext_data), .clock(clock));
  ROM rom_1 (.addr(print_num_1_address), .data(rom_1_data), .sel(1'b1));
  again_print_num again_print_num_1 (
    .exit_data(ext_data_3), .exit_data_2(ext_data), .sp_break(sp_break_3), .tag_1(tag_3),
    .not_exit_data(rom_1_data));
  ROM rom_2 (.addr(print_num_2_address), .data(rom_2_data), .sel(1'b1));
  again_print_num again_print_num_2 (
    .exit_data(ext_data_2), .exit_data_2(ext_data), .sp_break(sp_break_2), .tag_1(tag_2),
    .not_exit_data(rom_2_data));
  ROM rom_3 (.addr(print_num_3_address), .data(rom_3_data), .sel(1'b1));
  Register #(.width(16)) register_5 (.D(multiplexer_16_out), .Q(how_much), .clk(clock));  // open: en, clr
  again_print_num again_print_num_3 (
    .exit_data(ext_data_1), .exit_data_2(ext_data), .sp_break(sp_break_1), .tag_1(tag_1),
    .not_exit_data(rom_3_data));
  Multiplexer #(.width(16)) multiplexer_18 (
    .in0({{15{1'b0}}, wr_rd}), .in1(data_bus), .out(multiplexer_18_out), .sel(comparator_7_eq));  // open: en
  Comparator #(.width(16)) comparator_7 (.a(address_bus), .b(16'hfc00), .eq(comparator_7_eq));  // open: gt, lt
  not not_2 (from_signal, comparator_8_eq);
  Comparator #(.width(16), .mode("unsigned")) comparator_8 (
    .a({16{1'b0}}), .b(how_much), .eq(comparator_8_eq));  // open: gt, lt
  Random_store random_store_1 (
    .random_address(16'hfe00), .\break (\break ), .data_bus(data_bus), .address_bus(address_bus),
    .block(block), .clk(clk));
  // RAM ram_1: pin names not known; wires that end beside it: address_bus, data_bus
  mem_bar mem_bar_1 (
    .braek(\break ), .word(word), .clock(clock), .from_break(from_break), .mem(mem), .read(read));  // open: bit, sel, clock_2, ld, clear
  Register #(.width(1)) register_6 (.D(multiplexer_18_out[0]), .Q(wr_rd), .clk(clock));  // open: en, clr
  // Probe on address_bus
  // Probe on sp_break_3
  // UART uart_1: pin names not known; wires that end beside it: vec_adr, ext_data, out_1, out_2
  Pull_Resistor pull_resistor_11 (.node(\break ));
  Transistor #(.\type ("n")) transistor_21 (.in(1'b1), .out(\break ), .gate(wr_rd));
  // Probe on sp_break_4
  // Probe on sp_break_2
  // Probe on sp_break_1
  print_num print_num_4 (
    ._1_num(8'h23), ._2_num(8'h2a), ._3_num(8'h31), ._4_num(8'h38), .data_bus(data_bus),
    .address_bus(address_bus), .clock(clock), .exit_data(ext_data_4), .address(print_num_4_address),
    .sp_break(sp_break_4), .tag_1(tag_4), .break_point(8'h39), .start_add(16'hfc84));  // open: out_11, out_12
  ROM rom_4 (.addr(print_num_4_address), .data(rom_4_data), .sel(1'b1));
  telnet_bar telnet_bar_1 (.clock(clock), .rd_wr(wr_rd), .vec_adr(vec_adr));  // open: out_4, out_5, out_6
  again_print_num again_print_num_4 (
    .exit_data(ext_data_4), .exit_data_2(ext_data), .sp_break(sp_break_4), .tag_1(tag_4),
    .not_exit_data(rom_4_data));
  Multiplexer #(.width(16)) multiplexer_19 (
    .in0(register_7_q), .in1(data_bus), .out(multiplexer_19_out), .sel(comparator_9_eq));  // open: en
  Comparator #(.width(16)) comparator_9 (.a(address_bus), .b(16'hfc0c), .eq(comparator_9_eq));  // open: gt, lt
  Multiplexer #(.width(16)) multiplexer_20 (
    .in0(register_8_q), .in1(data_bus), .out(multiplexer_20_out), .sel(comparator_10_eq));  // open: en
  Comparator #(.width(16)) comparator_10 (.a(address_bus), .b(16'hfc04), .eq(comparator_10_eq));  // open: gt, lt
  // Probe on register_9_q
  Multiplexer #(.width(16)) multiplexer_21 (
    .in0(register_9_q), .in1(data_bus), .out(multiplexer_21_out), .sel(comparator_11_eq));  // open: en
  Comparator #(.width(16)) comparator_11 (.a(address_bus), .b(16'hfc10), .eq(comparator_11_eq));  // open: gt, lt
  // Probe on register_7_q
  Register #(.width(16)) register_7 (.D(multiplexer_19_out), .Q(register_7_q), .clk(clock));  // open: en, clr
  // Probe on register_8_q
  Register #(.width(16)) register_8 (.D(multiplexer_20_out), .Q(register_8_q), .clk(clock));  // open: en, clr
  Register #(.width(16)) register_9 (.D(multiplexer_21_out), .Q(register_9_q), .clk(clock));  // open: en, clr
  // Probe on register_10_q
  Register #(.width(16)) register_10 (.D(multiplexer_22_out), .Q(register_10_q), .clk(clock));  // open: en, clr
  Multiplexer #(.width(16)) multiplexer_22 (
    .in0(register_10_q), .in1(data_bus), .out(multiplexer_22_out), .sel(comparator_12_eq));  // open: en
  Comparator #(.width(16)) comparator_12 (.a(address_bus), .b(16'hfc0e), .eq(comparator_12_eq));  // open: gt, lt
  // Probe on register_11_q
  Register #(.width(16)) register_11 (.D(multiplexer_23_out), .Q(register_11_q), .clk(clock));  // open: en, clr
  Multiplexer #(.width(16)) multiplexer_23 (
    .in0(register_11_q), .in1(data_bus), .out(multiplexer_23_out), .sel(comparator_13_eq));  // open: en
  Comparator #(.width(16)) comparator_13 (.a(address_bus), .b(16'hfc06), .eq(comparator_13_eq));  // open: gt, lt
  // Probe on register_12_q
  Register #(.width(16)) register_12 (.D(multiplexer_24_out), .Q(register_12_q), .clk(clock));  // open: en, clr
  Multiplexer #(.width(16)) multiplexer_24 (
    .in0(register_12_q), .in1(data_bus), .out(multiplexer_24_out), .sel(comparator_14_eq));  // open: en
  Comparator #(.width(16)) comparator_14 (.a(address_bus), .b(16'hfc12), .eq(comparator_14_eq));  // open: gt, lt

  // Notes on the sheet:
  //    COMMAND HANDLER
  //   CDM16
  //   contents of rom_1 (hex, n*v repeats v):
  //   0 1b 5b 48 1b 5b 39 42 1b 5b 31 42 1b 5b 39 43 1b 5b 39 43 1b 5b 39 43 1b 5b 39 43 1b 5b 39 43 1b 5b
  //   39 43 1b 5b 31 43 20 1b 5b 44 1b 5b 44 20 1b 5b 44 1b 5b 44 20 1b 5b 44 1b 5b 44 20
  //   contents of rom_2 (hex, n*v repeats v):
  //   0 1b 5b 48 1b 5b 39 42 1b 5b 31 42 1b 5b 39 43 1b 5b 39 43 1b 5b 39 43 1b 5b 39 43 1b 5b 39 43 1b 5b
  //   39 43 1b 5b 36 43 20 1b 5b 44 1b 5b 44 20 1b 5b 44 1b 5b 44 20 1b 5b 44 1b 5b 44 20
  //   contents of rom_3 (hex, n*v repeats v):
  //   0 1b 5b 48 1b 5b 42 1b 5b 39 43 1b 5b 39 43 1b 5b 39 43 1b 5b 39 43 1b 5b 39 43 1b 5b 39 43 1b 5b 36
  //   43 20 1b 5b 32 44 20 1b 5b 32 44 20 1b 5b 32 44 20 1b 5b 32 44
  //   PROCESSOR INTERRUPTER
  //   Display balance and bid
  //   INTERFACE DISPLAY
  //   UART
  //   contents of rom_4 (hex, n*v repeats v):
  //   0 1b 5b 48 1b 5b 42 1b 5b 39 43 1b 5b 39 43 1b 5b 39 43 1b 5b 39 43 1b 5b 39 43 1b 5b 39 43 1b 5b 31
  //   43 20 1b 5b 44 1b 5b 44 20 1b 5b 44 1b 5b 44 20 1b 5b 44 1b 5b 44 20
  //   BOT
  //   bot's combination
  //   bot's bid
  //   BALANCE_BOT
  //   PLAYER
  //   BALANCE_PLAYER
  //   player's combination
  //   player's bid
endmodule

module Commands (
  input  [7:0] intput_value,
  input  clock,
  output [15:0] output_value
);

  wire comparator_1_eq, comparator_2_eq, comparator_3_eq, comparator_4_eq, comparator_5_eq, comparator_6_eq,
       not_1_out, not_2_out;
  wire [7:0] bet, call, check, fold, multiplexer_6_out, or_1_out, pull_resistor_1_node, pull_resistor_2_node,
       pull_resistor_3_node, pull_resistor_4_node, pull_resistor_5_node, raise;

  Comparator comparator_1 (.a(intput_value), .b(8'h62), .eq(comparator_1_eq));  // open: gt, lt
  Pull_Resistor pull_resistor_1 (.node(pull_resistor_1_node));
  Comparator comparator_2 (.a(intput_value), .b(8'h61), .eq(comparator_2_eq));  // open: gt, lt
  Pull_Resistor pull_resistor_2 (.node(pull_resistor_2_node));
  Multiplexer #(.width(8)) multiplexer_1 (
    .in0(pull_resistor_1_node), .in1(8'h5), .out(bet), .sel(comparator_1_eq));  // open: en
  Multiplexer #(.width(8)) multiplexer_2 (
    .in0(pull_resistor_2_node), .in1(8'h2), .out(call), .sel(comparator_2_eq));  // open: en
  Comparator comparator_3 (.a(intput_value), .b(8'h69), .eq(comparator_3_eq));  // open: gt, lt
  Pull_Resistor pull_resistor_3 (.node(pull_resistor_3_node));
  Comparator comparator_4 (.a(intput_value), .b(8'h68), .eq(comparator_4_eq));  // open: gt, lt
  Pull_Resistor pull_resistor_4 (.node(pull_resistor_4_node));
  Multiplexer #(.width(8)) multiplexer_3 (
    .in0(pull_resistor_3_node), .in1(8'h3), .out(raise), .sel(comparator_3_eq));  // open: en
  Multiplexer #(.width(8)) multiplexer_4 (
    .in0(pull_resistor_4_node), .in1(8'h4), .out(check), .sel(comparator_4_eq));  // open: en
  Comparator comparator_5 (.a(intput_value), .b(8'h66), .eq(comparator_5_eq));  // open: gt, lt
  Pull_Resistor pull_resistor_5 (.node(pull_resistor_5_node));
  Multiplexer #(.width(8)) multiplexer_5 (
    .in0(pull_resistor_5_node), .in1(8'h1), .out(fold), .sel(comparator_5_eq));  // open: en
  assign or_1_out = bet | call | raise | check | fold;  // OR_Gate or_1, 8 bits wide
  Register register_1 (.D(multiplexer_6_out), .Q(output_value[7:0]), .clk(not_1_out));  // open: en, clr
  Multiplexer #(.width(8)) multiplexer_6 (
    .in0(output_value[7:0]), .in1(or_1_out), .out(multiplexer_6_out), .sel(not_2_out));  // open: en
  not not_1 (not_1_out, clock);
  not not_2 (not_2_out, comparator_6_eq);
  Comparator comparator_6 (.a(or_1_out), .b({8{1'b0}}), .eq(comparator_6_eq));  // open: gt, lt

  assign output_value[15:8] = {8{1'b0}};

  // Other names for the same wires on the sheet: input_value[7:0] = intput_value
endmodule

module Bid (
  input  in_1,
  input  [7:0] in_2,
  output [15:0] out_3
);

  wire and_1_out, comparator_1_gt, comparator_2_lt, comparator_3_eq, not_1_out;
  wire [7:0] adder_1_out, multiplexer_1_out, multiplexer_2_out, multiplier_1_out, subtractor_1_out;

  Comparator comparator_1 (.a(in_2), .b(8'h29), .gt(comparator_1_gt));  // open: eq, lt
  Comparator comparator_2 (.a(in_2), .b(8'h40), .lt(comparator_2_lt));  // open: gt, eq
  and and_1 (and_1_out, comparator_1_gt, comparator_2_lt);
  Multiplexer #(.width(8)) multiplexer_1 (
    .in0({8{1'b0}}), .in1(subtractor_1_out), .out(multiplexer_1_out), .sel(and_1_out));  // open: en
  Subtractor subtractor_1 (.a(in_2), .b(8'h30), .out(subtractor_1_out));  // open: bin, bout
  Adder adder_1 (.a(multiplexer_2_out), .b(multiplexer_1_out), .out(adder_1_out));  // open: cin, cout
  not not_1 (not_1_out, in_1);
  Comparator comparator_3 (.a(in_2), .b({8{1'b0}}), .eq(comparator_3_eq));  // open: gt, lt
  Register register_1 (.D(adder_1_out), .Q(out_3[7:0]), .clk(not_1_out), .clr(comparator_3_eq));  // open: en
  Multiplexer #(.width(8)) multiplexer_2 (
    .in0(out_3[7:0]), .in1(multiplier_1_out), .out(multiplexer_2_out), .sel(and_1_out));  // open: en
  Multiplier multiplier_1 (.a(out_3[7:0]), .b(8'ha), .out(multiplier_1_out));  // open: cin, cout

  assign out_3[15:8] = {8{1'b0}};

  // Other names for the same wires on the sheet: input_num[7:0] = in_2; output_num[7:0] = out_3[7:0]
endmodule

module Randome_numbers (
  input  in_1,
  output [5:0] out_2,
  output [5:0] out_3,
  output [5:0] out_4,
  output [5:0] in_memory,
  output [5:0] out_6,
  output [5:0] out_7,
  output [5:0] out_8,
  output [5:0] out_9,
  output [5:0] out_10,
  output [5:0] out_11,
  output [5:0] out_12,
  output [5:0] out_13,
  output [5:0] out_14,
  output [5:0] out_15,
  output [5:0] out_16,
  output [5:0] out_17,
  output [5:0] out_18,
  output [5:0] out_19,
  output [5:0] out_20,
  output [5:0] out_21,
  output [5:0] out_22,
  output [5:0] out_23,
  output [5:0] out_24,
  output [5:0] out_25,
  output [5:0] out_26,
  output [5:0] out_27,
  output [5:0] out_28,
  output [5:0] out_29,
  output [5:0] out_30,
  output [5:0] out_31,
  output [5:0] out_32
);

  wire comparator_1_eq, comparator_2_eq, comparator_3_eq, comparator_4_eq, comparator_5_eq, comparator_6_eq,
       comparator_7_eq, comparator_8_eq, comparator_9_eq, comparator_10_eq, comparator_11_eq,
       comparator_12_eq, comparator_13_eq, comparator_14_eq, comparator_15_eq, comparator_16_eq,
       comparator_17_eq, comparator_18_eq, comparator_19_eq, comparator_20_eq, comparator_21_eq,
       comparator_22_eq, comparator_23_eq, comparator_24_eq, comparator_25_eq, comparator_26_eq,
       comparator_27_eq, comparator_28_eq, comparator_29_eq, comparator_30_eq, comparator_31_eq,
       comparator_32_eq, comparator_33_eq, comparator_34_eq, comparator_35_eq, comparator_36_eq,
       comparator_37_eq, comparator_38_gt, comparator_39_eq, comparator_40_eq, comparator_41_eq,
       comparator_42_eq, comparator_43_eq, comparator_44_eq, comparator_45_eq, comparator_46_eq,
       comparator_47_eq, comparator_48_eq, comparator_49_eq, comparator_50_eq, comparator_51_eq,
       comparator_52_eq, comparator_53_eq, comparator_54_eq, comparator_55_eq, comparator_56_eq,
       comparator_57_eq, comparator_58_eq, comparator_59_eq, comparator_60_eq, comparator_61_eq, first_or,
       not_1_out, not_2_out, not_3_out, not_4_out, not_5_out, not_6_out, not_7_out, not_8_out, not_9_out,
       not_10_out, not_11_out, not_12_out, not_13_out, not_14_out, not_15_out, not_16_out, not_17_out,
       not_18_out, not_19_out, not_20_out, not_21_out, not_22_out, not_23_out, not_24_out, not_25_out,
       not_26_out, not_27_out, not_28_out, not_29_out, or_4_out, or_5_out, second_or, third_or;
  wire [5:0] multiplexer_1_out, multiplexer_2_out, multiplexer_3_out, multiplexer_4_out, multiplexer_5_out,
       multiplexer_6_out, multiplexer_7_out, multiplexer_8_out, multiplexer_9_out, multiplexer_10_out,
       multiplexer_11_out, multiplexer_12_out, multiplexer_13_out, multiplexer_14_out, multiplexer_15_out,
       multiplexer_17_out, multiplexer_18_out, multiplexer_19_out, multiplexer_20_out, multiplexer_21_out,
       multiplexer_22_out, multiplexer_23_out, multiplexer_24_out, multiplexer_25_out, multiplexer_26_out,
       multiplexer_27_out, multiplexer_28_out, multiplexer_29_out, multiplexer_30_out, multiplexer_31_out,
       multiplexer_32_out, multiplexer_33_out, multiplexer_34_out, multiplexer_35_out, multiplexer_36_out,
       multiplexer_37_out, multiplexer_38_out, multiplexer_39_out, multiplexer_40_out, multiplexer_41_out,
       multiplexer_42_out, multiplexer_43_out, multiplexer_44_out, multiplexer_45_out, multiplexer_46_out,
       multiplexer_47_out, multiplexer_48_out, multiplexer_49_out, multiplexer_50_out, multiplexer_51_out,
       multiplexer_52_out, multiplexer_53_out, multiplexer_54_out, multiplexer_55_out, multiplexer_56_out,
       multiplexer_57_out, multiplexer_58_out, multiplexer_59_out, multiplexer_60_out, random_num;

  Multiplexer #(.width(6)) multiplexer_1 (
    .in0(out_2), .in1(in_memory), .out(multiplexer_1_out), .sel(comparator_31_eq));  // open: en
  Comparator #(.width(6)) comparator_1 (.a(out_2), .b(random_num), .eq(comparator_1_eq));  // open: gt, lt
  Comparator #(.width(6)) comparator_2 (.a(out_3), .b(random_num), .eq(comparator_2_eq));  // open: gt, lt
  Comparator #(.width(6)) comparator_3 (.a(out_4), .b(random_num), .eq(comparator_3_eq));  // open: gt, lt
  Comparator #(.width(6)) comparator_4 (.a(out_6), .b(random_num), .eq(comparator_4_eq));  // open: gt, lt
  Comparator #(.width(6)) comparator_5 (.a(out_7), .b(random_num), .eq(comparator_5_eq));  // open: gt, lt
  Comparator #(.width(6)) comparator_6 (.a(out_8), .b(random_num), .eq(comparator_6_eq));  // open: gt, lt
  Comparator #(.width(6)) comparator_7 (.a(out_9), .b(random_num), .eq(comparator_7_eq));  // open: gt, lt
  Comparator #(.width(6)) comparator_8 (.a(out_10), .b(random_num), .eq(comparator_8_eq));  // open: gt, lt
  Comparator #(.width(6)) comparator_9 (.a(out_11), .b(random_num), .eq(comparator_9_eq));  // open: gt, lt
  Comparator #(.width(6)) comparator_10 (.a(out_12), .b(random_num), .eq(comparator_10_eq));  // open: gt, lt
  Comparator #(.width(6)) comparator_11 (.a(out_13), .b(random_num), .eq(comparator_11_eq));  // open: gt, lt
  Comparator #(.width(6)) comparator_12 (.a(out_14), .b(random_num), .eq(comparator_12_eq));  // open: gt, lt
  Comparator #(.width(6)) comparator_13 (.a(out_15), .b(random_num), .eq(comparator_13_eq));  // open: gt, lt
  Comparator #(.width(6)) comparator_14 (.a(out_16), .b(random_num), .eq(comparator_14_eq));  // open: gt, lt
  Comparator #(.width(6)) comparator_15 (.a(out_17), .b(random_num), .eq(comparator_15_eq));  // open: gt, lt
  Comparator #(.width(6)) comparator_16 (.a(out_18), .b(random_num), .eq(comparator_16_eq));  // open: gt, lt
  Comparator #(.width(6)) comparator_17 (.a(out_19), .b(random_num), .eq(comparator_17_eq));  // open: gt, lt
  Comparator #(.width(6)) comparator_18 (.a(out_20), .b(random_num), .eq(comparator_18_eq));  // open: gt, lt
  Comparator #(.width(6)) comparator_19 (.a(out_21), .b(random_num), .eq(comparator_19_eq));  // open: gt, lt
  Comparator #(.width(6)) comparator_20 (.a(out_22), .b(random_num), .eq(comparator_20_eq));  // open: gt, lt
  Comparator #(.width(6)) comparator_21 (.a(out_23), .b(random_num), .eq(comparator_21_eq));  // open: gt, lt
  Comparator #(.width(6)) comparator_22 (.a(out_24), .b(random_num), .eq(comparator_22_eq));  // open: gt, lt
  Comparator #(.width(6)) comparator_23 (.a(out_25), .b(random_num), .eq(comparator_23_eq));  // open: gt, lt
  Comparator #(.width(6)) comparator_24 (.a(out_26), .b(random_num), .eq(comparator_24_eq));  // open: gt, lt
  Comparator #(.width(6)) comparator_25 (.a(out_27), .b(random_num), .eq(comparator_25_eq));  // open: gt, lt
  Comparator #(.width(6)) comparator_26 (.a(out_28), .b(random_num), .eq(comparator_26_eq));  // open: gt, lt
  Comparator #(.width(6)) comparator_27 (.a(out_29), .b(random_num), .eq(comparator_27_eq));  // open: gt, lt
  Comparator #(.width(6)) comparator_28 (.a(out_30), .b(random_num), .eq(comparator_28_eq));  // open: gt, lt
  Comparator #(.width(6)) comparator_29 (.a(out_31), .b(random_num), .eq(comparator_29_eq));  // open: gt, lt
  Comparator #(.width(6)) comparator_30 (.a(out_32), .b(random_num), .eq(comparator_30_eq));  // open: gt, lt
  Register #(.width(6)) register_1 (.D(multiplexer_1_out), .Q(out_2), .clk(in_1));  // open: en, clr
  Comparator #(.width(6)) comparator_31 (.a(out_2), .b({6{1'b0}}), .eq(comparator_31_eq));  // open: gt, lt
  not not_1 (not_1_out, comparator_31_eq);
  Multiplexer #(.width(6)) multiplexer_2 (
    .in0(out_3), .in1(multiplexer_3_out), .out(multiplexer_2_out), .sel(not_1_out));  // open: en
  Multiplexer #(.width(6)) multiplexer_3 (
    .in0(out_3), .in1(in_memory), .out(multiplexer_3_out), .sel(comparator_32_eq));  // open: en
  Register #(.width(6)) register_2 (.D(multiplexer_2_out), .Q(out_3), .clk(in_1));  // open: en, clr
  Comparator #(.width(6)) comparator_32 (.a(out_3), .b({6{1'b0}}), .eq(comparator_32_eq));  // open: gt, lt
  not not_2 (not_2_out, comparator_32_eq);
  Multiplexer #(.width(6)) multiplexer_4 (
    .in0(out_4), .in1(in_memory), .out(multiplexer_4_out), .sel(comparator_33_eq));  // open: en
  or or_1 (first_or, comparator_1_eq, comparator_2_eq, comparator_3_eq, comparator_4_eq, comparator_5_eq, comparator_6_eq, comparator_7_eq, comparator_8_eq, comparator_9_eq, comparator_10_eq);
  or or_2 (second_or, comparator_11_eq, comparator_12_eq, comparator_13_eq, comparator_14_eq, comparator_15_eq, comparator_16_eq, comparator_17_eq, comparator_18_eq, comparator_19_eq, comparator_20_eq);
  or or_3 (third_or, comparator_21_eq, comparator_22_eq, comparator_23_eq, comparator_24_eq, comparator_25_eq, comparator_26_eq, comparator_27_eq, comparator_28_eq, comparator_29_eq, comparator_30_eq);
  Multiplexer #(.width(6)) multiplexer_5 (
    .in0(out_4), .in1(multiplexer_4_out), .out(multiplexer_5_out), .sel(not_2_out));  // open: en
  Register #(.width(6)) register_3 (.D(multiplexer_5_out), .Q(out_4), .clk(in_1));  // open: en, clr
  Comparator #(.width(6)) comparator_33 (.a(out_4), .b({6{1'b0}}), .eq(comparator_33_eq));  // open: gt, lt
  not not_3 (not_3_out, comparator_33_eq);
  Multiplexer #(.width(6)) multiplexer_6 (
    .in0(out_6), .in1(multiplexer_7_out), .out(multiplexer_6_out), .sel(not_3_out));  // open: en
  Multiplexer #(.width(6)) multiplexer_7 (
    .in0(out_6), .in1(in_memory), .out(multiplexer_7_out), .sel(comparator_34_eq));  // open: en
  Register #(.width(6)) register_4 (.D(multiplexer_6_out), .Q(out_6), .clk(in_1));  // open: en, clr
  Multiplexer #(.width(6)) multiplexer_8 (
    .in0(out_7), .in1(in_memory), .out(multiplexer_8_out), .sel(comparator_35_eq));  // open: en
  Comparator #(.width(6)) comparator_34 (.a(out_6), .b({6{1'b0}}), .eq(comparator_34_eq));  // open: gt, lt
  not not_4 (not_4_out, comparator_34_eq);
  Register #(.width(6)) register_5 (.D(multiplexer_9_out), .Q(out_7), .clk(in_1));  // open: en, clr
  Multiplexer #(.width(6)) multiplexer_9 (
    .in0(out_7), .in1(multiplexer_8_out), .out(multiplexer_9_out), .sel(not_4_out));  // open: en
  Comparator #(.width(6)) comparator_35 (.a(out_7), .b({6{1'b0}}), .eq(comparator_35_eq));  // open: gt, lt
  not not_5 (not_5_out, comparator_35_eq);
  Multiplexer #(.width(6)) multiplexer_10 (
    .in0(out_8), .in1(in_memory), .out(multiplexer_10_out), .sel(comparator_36_eq));  // open: en
  Multiplexer #(.width(6)) multiplexer_11 (
    .in0(out_8), .in1(multiplexer_10_out), .out(multiplexer_11_out), .sel(not_5_out));  // open: en
  Register #(.width(6)) register_6 (.D(multiplexer_11_out), .Q(out_8), .clk(in_1));  // open: en, clr
  Random #(.width(6)) random_1 (.clk(in_1), .out(random_num));  // open: next, clr
  Comparator #(.width(6)) comparator_36 (.a(out_8), .b({6{1'b0}}), .eq(comparator_36_eq));  // open: gt, lt
  not not_6 (not_6_out, comparator_36_eq);
  Multiplexer #(.width(6)) multiplexer_12 (
    .in0(out_9), .in1(multiplexer_13_out), .out(multiplexer_12_out), .sel(not_6_out));  // open: en
  Multiplexer #(.width(6)) multiplexer_13 (
    .in0(out_9), .in1(in_memory), .out(multiplexer_13_out), .sel(comparator_37_eq));  // open: en
  Register #(.width(6)) register_7 (.D(multiplexer_12_out), .Q(out_9), .clk(in_1));  // open: en, clr
  Comparator #(.width(6)) comparator_37 (.a(out_9), .b({6{1'b0}}), .eq(comparator_37_eq));  // open: gt, lt
  Multiplexer #(.width(6)) multiplexer_14 (
    .in0(out_10), .in1(in_memory), .out(multiplexer_14_out), .sel(comparator_39_eq));  // open: en
  or or_4 (or_4_out, first_or, second_or, third_or);
  Comparator #(.width(6), .mode("unsigned")) comparator_38 (
    .a(random_num), .b(6'b110100), .gt(comparator_38_gt));  // open: eq, lt
  not not_7 (not_7_out, comparator_37_eq);
  Multiplexer #(.width(6)) multiplexer_15 (
    .in0(out_10), .in1(multiplexer_14_out), .out(multiplexer_15_out), .sel(not_7_out));  // open: en
  Register #(.width(6)) register_8 (.D(multiplexer_15_out), .Q(out_10), .clk(in_1));  // open: en, clr
  Multiplexer #(.width(6)) multiplexer_16 (
    .in0(random_num), .in1({6{1'b0}}), .out(in_memory), .sel(or_5_out));  // open: en
  or or_5 (or_5_out, or_4_out, comparator_38_gt);
  Comparator #(.width(6)) comparator_39 (.a(out_10), .b({6{1'b0}}), .eq(comparator_39_eq));  // open: gt, lt
  not not_8 (not_8_out, comparator_39_eq);
  Multiplexer #(.width(6)) multiplexer_17 (
    .in0(out_11), .in1(multiplexer_18_out), .out(multiplexer_17_out), .sel(not_8_out));  // open: en
  Multiplexer #(.width(6)) multiplexer_18 (
    .in0(out_11), .in1(in_memory), .out(multiplexer_18_out), .sel(comparator_40_eq));  // open: en
  Pull_Resistor pull_resistor_1 (.node(in_memory));
  Register #(.width(6)) register_9 (.D(multiplexer_17_out), .Q(out_11), .clk(in_1));  // open: en, clr
  Comparator #(.width(6)) comparator_40 (.a(out_11), .b({6{1'b0}}), .eq(comparator_40_eq));  // open: gt, lt
  not not_9 (not_9_out, comparator_40_eq);
  Multiplexer #(.width(6)) multiplexer_19 (
    .in0(out_12), .in1(multiplexer_20_out), .out(multiplexer_19_out), .sel(not_9_out));  // open: en
  Multiplexer #(.width(6)) multiplexer_20 (
    .in0(out_12), .in1(in_memory), .out(multiplexer_20_out), .sel(comparator_41_eq));  // open: en
  Register #(.width(6)) register_10 (.D(multiplexer_19_out), .Q(out_12), .clk(in_1));  // open: en, clr
  Comparator #(.width(6)) comparator_41 (.a(out_12), .b({6{1'b0}}), .eq(comparator_41_eq));  // open: gt, lt
  not not_10 (not_10_out, comparator_41_eq);
  Multiplexer #(.width(6)) multiplexer_21 (
    .in0(out_13), .in1(in_memory), .out(multiplexer_21_out), .sel(comparator_42_eq));  // open: en
  Multiplexer #(.width(6)) multiplexer_22 (
    .in0(out_13), .in1(multiplexer_21_out), .out(multiplexer_22_out), .sel(not_10_out));  // open: en
  Register #(.width(6)) register_11 (.D(multiplexer_22_out), .Q(out_13), .clk(in_1));  // open: en, clr
  Comparator #(.width(6)) comparator_42 (.a(out_13), .b({6{1'b0}}), .eq(comparator_42_eq));  // open: gt, lt
  not not_11 (not_11_out, comparator_42_eq);
  Multiplexer #(.width(6)) multiplexer_23 (
    .in0(out_14), .in1(multiplexer_24_out), .out(multiplexer_23_out), .sel(not_11_out));  // open: en
  Multiplexer #(.width(6)) multiplexer_24 (
    .in0(out_14), .in1(in_memory), .out(multiplexer_24_out), .sel(comparator_43_eq));  // open: en
  Register #(.width(6)) register_12 (.D(multiplexer_23_out), .Q(out_14), .clk(in_1));  // open: en, clr
  Multiplexer #(.width(6)) multiplexer_25 (
    .in0(out_15), .in1(in_memory), .out(multiplexer_25_out), .sel(comparator_44_eq));  // open: en
  Comparator #(.width(6)) comparator_43 (.a(out_14), .b({6{1'b0}}), .eq(comparator_43_eq));  // open: gt, lt
  not not_12 (not_12_out, comparator_43_eq);
  Multiplexer #(.width(6)) multiplexer_26 (
    .in0(out_15), .in1(multiplexer_25_out), .out(multiplexer_26_out), .sel(not_12_out));  // open: en
  Register #(.width(6)) register_13 (.D(multiplexer_26_out), .Q(out_15), .clk(in_1));  // open: en, clr
  Comparator #(.width(6)) comparator_44 (.a(out_15), .b({6{1'b0}}), .eq(comparator_44_eq));  // open: gt, lt
  not not_13 (not_13_out, comparator_44_eq);
  Multiplexer #(.width(6)) multiplexer_27 (
    .in0(out_16), .in1(in_memory), .out(multiplexer_27_out), .sel(comparator_45_eq));  // open: en
  Register #(.width(6)) register_14 (.D(multiplexer_28_out), .Q(out_16), .clk(in_1));  // open: en, clr
  Multiplexer #(.width(6)) multiplexer_28 (
    .in0(out_16), .in1(multiplexer_27_out), .out(multiplexer_28_out), .sel(not_13_out));  // open: en
  Comparator #(.width(6)) comparator_45 (.a(out_16), .b({6{1'b0}}), .eq(comparator_45_eq));  // open: gt, lt
  not not_14 (not_14_out, comparator_45_eq);
  Multiplexer #(.width(6)) multiplexer_29 (
    .in0(out_17), .in1(multiplexer_30_out), .out(multiplexer_29_out), .sel(not_14_out));  // open: en
  Multiplexer #(.width(6)) multiplexer_30 (
    .in0(out_17), .in1(in_memory), .out(multiplexer_30_out), .sel(comparator_46_eq));  // open: en
  Register #(.width(6)) register_15 (.D(multiplexer_29_out), .Q(out_17), .clk(in_1));  // open: en, clr
  Comparator #(.width(6)) comparator_46 (.a(out_17), .b({6{1'b0}}), .eq(comparator_46_eq));  // open: gt, lt
  Multiplexer #(.width(6)) multiplexer_31 (
    .in0(out_18), .in1(in_memory), .out(multiplexer_31_out), .sel(comparator_47_eq));  // open: en
  not not_15 (not_15_out, comparator_46_eq);
  Multiplexer #(.width(6)) multiplexer_32 (
    .in0(out_18), .in1(multiplexer_31_out), .out(multiplexer_32_out), .sel(not_15_out));  // open: en
  Register #(.width(6)) register_16 (.D(multiplexer_32_out), .Q(out_18), .clk(in_1));  // open: en, clr
  Comparator #(.width(6)) comparator_47 (.a(out_18), .b({6{1'b0}}), .eq(comparator_47_eq));  // open: gt, lt
  not not_16 (not_16_out, comparator_47_eq);
  Multiplexer #(.width(6)) multiplexer_33 (
    .in0(out_19), .in1(multiplexer_34_out), .out(multiplexer_33_out), .sel(not_16_out));  // open: en
  Multiplexer #(.width(6)) multiplexer_34 (
    .in0(out_19), .in1(in_memory), .out(multiplexer_34_out), .sel(comparator_48_eq));  // open: en
  Register #(.width(6)) register_17 (.D(multiplexer_33_out), .Q(out_19), .clk(in_1));  // open: en, clr
  Comparator #(.width(6)) comparator_48 (.a(out_19), .b({6{1'b0}}), .eq(comparator_48_eq));  // open: gt, lt
  not not_17 (not_17_out, comparator_48_eq);
  Multiplexer #(.width(6)) multiplexer_35 (
    .in0(out_20), .in1(multiplexer_36_out), .out(multiplexer_35_out), .sel(not_17_out));  // open: en
  Multiplexer #(.width(6)) multiplexer_36 (
    .in0(out_20), .in1(in_memory), .out(multiplexer_36_out), .sel(comparator_49_eq));  // open: en
  Register #(.width(6)) register_18 (.D(multiplexer_35_out), .Q(out_20), .clk(in_1));  // open: en, clr
  Comparator #(.width(6)) comparator_49 (.a(out_20), .b({6{1'b0}}), .eq(comparator_49_eq));  // open: gt, lt
  not not_18 (not_18_out, comparator_49_eq);
  Multiplexer #(.width(6)) multiplexer_37 (
    .in0(out_21), .in1(in_memory), .out(multiplexer_37_out), .sel(comparator_50_eq));  // open: en
  Register #(.width(6)) register_19 (.D(multiplexer_38_out), .Q(out_21), .clk(in_1));  // open: en, clr
  Multiplexer #(.width(6)) multiplexer_38 (
    .in0(out_21), .in1(multiplexer_37_out), .out(multiplexer_38_out), .sel(not_18_out));  // open: en
  Comparator #(.width(6)) comparator_50 (.a(out_21), .b({6{1'b0}}), .eq(comparator_50_eq));  // open: gt, lt
  not not_19 (not_19_out, comparator_50_eq);
  Multiplexer #(.width(6)) multiplexer_39 (
    .in0(out_22), .in1(multiplexer_40_out), .out(multiplexer_39_out), .sel(not_19_out));  // open: en
  Multiplexer #(.width(6)) multiplexer_40 (
    .in0(out_22), .in1(in_memory), .out(multiplexer_40_out), .sel(comparator_51_eq));  // open: en
  Register #(.width(6)) register_20 (.D(multiplexer_39_out), .Q(out_22), .clk(in_1));  // open: en, clr
  Multiplexer #(.width(6)) multiplexer_41 (
    .in0(out_23), .in1(in_memory), .out(multiplexer_41_out), .sel(comparator_52_eq));  // open: en
  Comparator #(.width(6)) comparator_51 (.a(out_22), .b({6{1'b0}}), .eq(comparator_51_eq));  // open: gt, lt
  not not_20 (not_20_out, comparator_51_eq);
  Register #(.width(6)) register_21 (.D(multiplexer_42_out), .Q(out_23), .clk(in_1));  // open: en, clr
  Multiplexer #(.width(6)) multiplexer_42 (
    .in0(out_23), .in1(multiplexer_41_out), .out(multiplexer_42_out), .sel(not_20_out));  // open: en
  Comparator #(.width(6)) comparator_52 (.a(out_23), .b({6{1'b0}}), .eq(comparator_52_eq));  // open: gt, lt
  not not_21 (not_21_out, comparator_52_eq);
  Multiplexer #(.width(6)) multiplexer_43 (
    .in0(out_24), .in1(in_memory), .out(multiplexer_43_out), .sel(comparator_53_eq));  // open: en
  Register #(.width(6)) register_22 (.D(multiplexer_44_out), .Q(out_24), .clk(in_1));  // open: en, clr
  Multiplexer #(.width(6)) multiplexer_44 (
    .in0(out_24), .in1(multiplexer_43_out), .out(multiplexer_44_out), .sel(not_21_out));  // open: en
  Comparator #(.width(6)) comparator_53 (.a(out_24), .b({6{1'b0}}), .eq(comparator_53_eq));  // open: gt, lt
  not not_22 (not_22_out, comparator_53_eq);
  Multiplexer #(.width(6)) multiplexer_45 (
    .in0(out_25), .in1(multiplexer_46_out), .out(multiplexer_45_out), .sel(not_22_out));  // open: en
  Multiplexer #(.width(6)) multiplexer_46 (
    .in0(out_25), .in1(in_memory), .out(multiplexer_46_out), .sel(comparator_54_eq));  // open: en
  Register #(.width(6)) register_23 (.D(multiplexer_45_out), .Q(out_25), .clk(in_1));  // open: en, clr
  Comparator #(.width(6)) comparator_54 (.a(out_25), .b({6{1'b0}}), .eq(comparator_54_eq));  // open: gt, lt
  Multiplexer #(.width(6)) multiplexer_47 (
    .in0(out_26), .in1(in_memory), .out(multiplexer_47_out), .sel(comparator_55_eq));  // open: en
  not not_23 (not_23_out, comparator_54_eq);
  Multiplexer #(.width(6)) multiplexer_48 (
    .in0(out_26), .in1(multiplexer_47_out), .out(multiplexer_48_out), .sel(not_23_out));  // open: en
  Register #(.width(6)) register_24 (.D(multiplexer_48_out), .Q(out_26), .clk(in_1));  // open: en, clr
  Comparator #(.width(6)) comparator_55 (.a(out_26), .b({6{1'b0}}), .eq(comparator_55_eq));  // open: gt, lt
  not not_24 (not_24_out, comparator_55_eq);
  Multiplexer #(.width(6)) multiplexer_49 (
    .in0(out_27), .in1(multiplexer_50_out), .out(multiplexer_49_out), .sel(not_24_out));  // open: en
  Multiplexer #(.width(6)) multiplexer_50 (
    .in0(out_27), .in1(in_memory), .out(multiplexer_50_out), .sel(comparator_56_eq));  // open: en
  Register #(.width(6)) register_25 (.D(multiplexer_49_out), .Q(out_27), .clk(in_1));  // open: en, clr
  Comparator #(.width(6)) comparator_56 (.a(out_27), .b({6{1'b0}}), .eq(comparator_56_eq));  // open: gt, lt
  not not_25 (not_25_out, comparator_56_eq);
  Multiplexer #(.width(6)) multiplexer_51 (
    .in0(out_28), .in1(multiplexer_52_out), .out(multiplexer_51_out), .sel(not_25_out));  // open: en
  Multiplexer #(.width(6)) multiplexer_52 (
    .in0(out_28), .in1(in_memory), .out(multiplexer_52_out), .sel(comparator_57_eq));  // open: en
  Register #(.width(6)) register_26 (.D(multiplexer_51_out), .Q(out_28), .clk(in_1));  // open: en, clr
  Comparator #(.width(6)) comparator_57 (.a(out_28), .b({6{1'b0}}), .eq(comparator_57_eq));  // open: gt, lt
  not not_26 (not_26_out, comparator_57_eq);
  Multiplexer #(.width(6)) multiplexer_53 (
    .in0(out_29), .in1(in_memory), .out(multiplexer_53_out), .sel(comparator_58_eq));  // open: en
  Register #(.width(6)) register_27 (.D(multiplexer_54_out), .Q(out_29), .clk(in_1));  // open: en, clr
  Multiplexer #(.width(6)) multiplexer_54 (
    .in0(out_29), .in1(multiplexer_53_out), .out(multiplexer_54_out), .sel(not_26_out));  // open: en
  Comparator #(.width(6)) comparator_58 (.a(out_29), .b({6{1'b0}}), .eq(comparator_58_eq));  // open: gt, lt
  not not_27 (not_27_out, comparator_58_eq);
  Multiplexer #(.width(6)) multiplexer_55 (
    .in0(out_30), .in1(multiplexer_56_out), .out(multiplexer_55_out), .sel(not_27_out));  // open: en
  Multiplexer #(.width(6)) multiplexer_56 (
    .in0(out_30), .in1(in_memory), .out(multiplexer_56_out), .sel(comparator_59_eq));  // open: en
  Register #(.width(6)) register_28 (.D(multiplexer_55_out), .Q(out_30), .clk(in_1));  // open: en, clr
  Multiplexer #(.width(6)) multiplexer_57 (
    .in0(out_31), .in1(in_memory), .out(multiplexer_57_out), .sel(comparator_60_eq));  // open: en
  Comparator #(.width(6)) comparator_59 (.a(out_30), .b({6{1'b0}}), .eq(comparator_59_eq));  // open: gt, lt
  not not_28 (not_28_out, comparator_59_eq);
  Register #(.width(6)) register_29 (.D(multiplexer_58_out), .Q(out_31), .clk(in_1));  // open: en, clr
  Multiplexer #(.width(6)) multiplexer_58 (
    .in0(out_31), .in1(multiplexer_57_out), .out(multiplexer_58_out), .sel(not_28_out));  // open: en
  Comparator #(.width(6)) comparator_60 (.a(out_31), .b({6{1'b0}}), .eq(comparator_60_eq));  // open: gt, lt
  not not_29 (not_29_out, comparator_60_eq);
  Multiplexer #(.width(6)) multiplexer_59 (
    .in0(out_32), .in1(in_memory), .out(multiplexer_59_out), .sel(comparator_61_eq));  // open: en
  Register #(.width(6)) register_30 (.D(multiplexer_60_out), .Q(out_32), .clk(in_1));  // open: en, clr
  Multiplexer #(.width(6)) multiplexer_60 (
    .in0(out_32), .in1(multiplexer_59_out), .out(multiplexer_60_out), .sel(not_29_out));  // open: en
  Comparator #(.width(6)) comparator_61 (.a(out_32), .b({6{1'b0}}), .eq(comparator_61_eq));  // open: gt, lt

  // Other names for the same wires on the sheet: _1r[5:0] = out_2; _2r[5:0] = out_3; _3r[5:0] = out_4;
  //   _4r[5:0] = out_6; _5r[5:0] = out_7; _6r[5:0] = out_8; _7r[5:0] = out_9; _8r[5:0] = out_10; _9r[5:0] = out_11;
  //   _10r[5:0] = out_12; _11r[5:0] = out_13; _12r[5:0] = out_14; _13r[5:0] = out_15; _14r[5:0] = out_16;
  //   _15r[5:0] = out_17; _16r[5:0] = out_18; _17r[5:0] = out_19; _18r[5:0] = out_20; _19r[5:0] = out_21;
  //   _20r[5:0] = out_22; _21r[5:0] = out_23; _22r[5:0] = out_24; _23r[5:0] = out_25; _24r[5:0] = out_26;
  //   _25r[5:0] = out_27; _26r[5:0] = out_28; _27r[5:0] = out_29; _28r[5:0] = out_30; _29r[5:0] = out_31;
  //   _30r[5:0] = out_32; cclock = in_1; check_random_num[5:0] = in_memory
endmodule

module Random_store (
  input  [15:0] random_address,
  input  clk,
  output \break ,
  output [15:0] data_bus,
  output block,
  output [15:0] address_bus
);

  wire clock, comparator_2_eq, comparator_3_eq, not_1_out, register_3_q, register_4_q;
  wire [5:0] _1r, _2r, _3r, _4r, _5r, _6r, _7r, _8r, _9r, _10r, _11r, _12r, _13r, _14r, _15r, _16r, _17r,
       _18r, _19r, _20r, _21r, _22r, _23r, _24r, _25r, _26r, _27r, _28r, _29r, _30r, in_memory,
       randome_numbers_1_in_memory;
  wire [15:0] adder_1_out, adder_2_out, multiplexer_1_out, multiplexer_2_out, multiplexer_3_out,
       register_2_q, subtractor_1_out;

  Adder #(.width(16)) adder_1 (.a(random_address), .b(16'h3c), .out(adder_1_out));  // open: cin, cout
  Adder #(.width(16)) adder_2 (.a(register_2_q), .b(16'h2), .out(adder_2_out));  // open: cin, cout
  Comparator #(.width(16), .mode("unsigned")) comparator_1 (
    .a(adder_1_out), .b(register_2_q), .gt(block));  // open: eq, lt
  Multiplexer #(.width(16)) multiplexer_1 (
    .in0(register_2_q), .in1(adder_2_out), .out(multiplexer_1_out), .sel(not_1_out));  // open: en
  Comparator #(.width(6), .mode("unsigned")) comparator_2 (
    .a(in_memory), .b({6{1'b0}}), .eq(comparator_2_eq));  // open: gt, lt
  not not_1 (not_1_out, comparator_2_eq);
  Transistor #(.\type ("n")) transistor_1 (.in(block), .out(\break ), .gate(block));
  Randome_numbers randome_numbers_1 (
    .in_1(clock), .out_2(_1r), .out_3(_2r), .out_4(_3r), .out_6(_4r), .out_7(_5r), .out_8(_6r), .out_9(_7r),
    .out_10(_8r), .out_11(_9r), .out_12(_10r), .out_13(_11r), .out_14(_12r), .out_15(_13r), .out_16(_14r),
    .out_17(_15r), .out_18(_16r), .out_19(_17r), .out_20(_18r), .out_21(_19r), .out_22(_20r), .out_23(_21r),
    .out_24(_22r), .out_25(_23r), .out_26(_24r), .out_27(_25r), .out_28(_26r), .out_29(_27r), .out_30(_28r),
    .out_31(_29r), .out_32(_30r), .in_memory(randome_numbers_1_in_memory));
  Subtractor #(.width(16)) subtractor_1 (
    .a({{10{1'b0}}, in_memory}), .b(16'h1), .out(subtractor_1_out));  // open: bin, bout
  Comparator #(.width(16), .mode("unsigned")) comparator_3 (
    .a(register_2_q), .b({16{1'b0}}), .eq(comparator_3_eq));  // open: gt, lt
  Multiplexer #(.width(16)) multiplexer_2 (
    .in0(multiplexer_1_out), .in1(random_address), .out(multiplexer_2_out), .sel(comparator_3_eq));  // open: en
  // Probe on in_memory
  Register #(.width(6)) register_1 (.D(randome_numbers_1_in_memory), .Q(in_memory), .clk(clock));  // open: en, clr
  Transistor #(.\type ("n"), .width(16)) transistor_2 (.in(subtractor_1_out), .out(data_bus), .gate(block));
  Multiplexer #(.width(16)) multiplexer_3 (
    .in0(register_2_q), .in1(multiplexer_2_out), .out(multiplexer_3_out), .sel(block));  // open: en
  Register #(.width(16)) register_2 (.D(multiplexer_3_out), .Q(register_2_q), .clk(clk));  // open: en, clr
  Register #(.width(1)) register_3 (.D(1'b1), .Q(register_3_q), .clk(clk));  // open: en, clr
  Transistor #(.\type ("n"), .width(16)) transistor_3 (.in(register_2_q), .out(address_bus), .gate(block));
  Transistor #(.\type ("n")) transistor_4 (.in(clk), .out(clock), .gate(register_4_q));
  Pull_Resistor pull_resistor_1 (.node(clock));
  Register #(.width(1)) register_4 (.D(register_3_q), .Q(register_4_q), .clk(clk));  // open: en, clr
endmodule

module telnet_bar (
  input  clock,
  input  [7:0] vec_adr,
  input  rd_wr,
  output out_4,
  output out_5,
  output out_6
);

  wire comparator_1_eq;

  or or_1 (out_4, comparator_1_eq, rd_wr);
  Comparator comparator_1 (.a(vec_adr), .b(8'ha), .eq(comparator_1_eq));  // open: gt, lt

  assign out_5 = clock;
  assign out_6 = 1'b1;
endmodule

module \interface  (
  input  clock,
  output [7:0] exit_data
);

  wire comparator_1_eq;
  wire [7:0] undriven;
  wire [15:0] adder_1_out, multiplexer_1_out, register_1_q;

  Adder #(.width(16)) adder_1 (.a(register_1_q), .b(16'h1), .out(adder_1_out));  // open: cin, cout
  Comparator #(.width(16)) comparator_1 (.a(16'h7bc), .b(register_1_q), .eq(comparator_1_eq));  // open: gt, lt
  // Probe on multiplexer_1_out
  Multiplexer #(.width(16)) multiplexer_1 (
    .in0(adder_1_out), .in1(register_1_q), .out(multiplexer_1_out), .sel(comparator_1_eq));  // open: en
  Register #(.width(16)) register_1 (.D(multiplexer_1_out), .Q(register_1_q), .clk(clock));  // open: en, clr
  // ROM rom_1: pin names not known; wires that end beside it: register_1_q, 1'b1
  // Probe on exit_data
  Transistor #(.width(8)) transistor_1 (.in(undriven), .out(exit_data), .gate(comparator_1_eq));
endmodule

module mem_bar (
  input  braek,
  input  word,
  input  clock,
  input  from_break,
  input  mem,
  input  read,
  output \bit ,
  output sel,
  output clock_2,
  output ld,
  output clear
);

  wire multiplexer_3_out, multiplexer_5_out, not_1_out, register_1_q, telnet;

  Multiplexer multiplexer_1 (.in0(word), .in1(1'b1), .out(\bit ), .sel(braek));  // open: en
  Multiplexer multiplexer_2 (.in0(multiplexer_3_out), .in1(1'b1), .out(sel), .sel(from_break));  // open: en
  Multiplexer multiplexer_3 (.in0(mem), .in1(not_1_out), .out(multiplexer_3_out), .sel(braek));  // open: en
  not not_1 (not_1_out, register_1_q);
  Register #(.width(1)) register_1 (.D(telnet), .Q(register_1_q), .clk(clock));  // open: en, clr
  Multiplexer multiplexer_4 (.in0(multiplexer_5_out), .in1(1'b1), .out(ld), .sel(from_break));  // open: en
  Multiplexer multiplexer_5 (.in0(read), .in1(register_1_q), .out(multiplexer_5_out), .sel(braek));  // open: en

  assign clear = 1'b0;
  assign clock_2 = clock;

  // Other names for the same wires on the sheet: break = braek
endmodule

module cdm_power (
  input  from_signal,
  input  \break ,
  input  clock,
  output out_4
);

  wire multiplexer_2_out;

  Multiplexer multiplexer_1 (.in0(multiplexer_2_out), .in1(1'b0), .out(out_4), .sel(from_signal));  // open: en
  Multiplexer multiplexer_2 (.in0(clock), .in1(1'b0), .out(multiplexer_2_out), .sel(\break ));  // open: en
endmodule

module cdm_bar (
  input  mem,
  input  read,
  input  word,
  input  [15:0] addr,
  input  \break ,
  output mem_2,
  output read_2,
  output word_2,
  output [15:0] address_bus
);

  Multiplexer #(.width(16)) multiplexer_1 (.in0(addr), .out(address_bus), .sel(\break ));  // open: in1, en

  assign mem_2 = mem;
  assign read_2 = read;
  assign word_2 = word;
endmodule

module terminal_write (
  input  clock,
  input  block,
  input  [15:0] address_bus,
  input  [15:0] data_bus,
  output from_break,
  output from_signal,
  output telnet,
  output \break ,
  output [7:0] ext_data,
  output [15:0] address_bus_2,
  output [15:0] data_bus_2
);

  wire comparator_1_eq, comparator_2_eq, comparator_3_eq, comparator_3_gt, comparator_3_lt, comparator_4_eq,
       or_1_out, pull_resistor_2_node, transistor_4_out;
  wire [15:0] adder_1_out, adder_2_out, from, how_much, multiplexer_1_out, multiplexer_2_out,
       multiplexer_3_out, multiplexer_4_out, multiplexer_5_out, pull_resistor_1_node, register_1_q;
  wire [15:8] transistor_6_out;

  Pull_Resistor pull_resistor_1 (.node(pull_resistor_1_node));
  Adder #(.width(16)) adder_1 (.a(from), .b(how_much), .out(adder_1_out));  // open: cin, cout
  Transistor #(.\type ("n"), .width(16)) transistor_1 (
    .in(register_1_q), .out(pull_resistor_1_node), .gate(from_break));
  Multiplexer #(.width(16)) multiplexer_1 (
    .in0(from), .in1(adder_2_out), .out(multiplexer_1_out), .sel(from_signal));  // open: en
  Adder #(.width(16)) adder_2 (.a(pull_resistor_1_node), .b(16'h2), .out(adder_2_out));  // open: cin, cout
  Comparator #(.width(16)) comparator_1 (.a(address_bus), .b(16'hfc1a), .eq(comparator_1_eq));  // open: gt, lt
  Comparator #(.width(16)) comparator_2 (.a(address_bus), .b(16'hfc1c), .eq(comparator_2_eq));  // open: gt, lt
  Comparator #(.width(16), .mode("unsigned")) comparator_3 (
    .a(adder_1_out), .b(register_1_q), .gt(comparator_3_gt), .eq(comparator_3_eq), .lt(comparator_3_lt));
  Register #(.width(16)) register_1 (.D(multiplexer_1_out), .Q(register_1_q), .clk(clock));  // open: en, clr
  Multiplexer #(.width(16)) multiplexer_2 (
    .in0(from), .in1(multiplexer_3_out), .out(multiplexer_2_out), .sel(comparator_1_eq));  // open: en
  Multiplexer #(.width(16)) multiplexer_3 (
    .in0({16{1'b0}}), .out(multiplexer_3_out), .sel(comparator_1_eq));  // open: in1, en
  Multiplexer #(.width(16)) multiplexer_4 (
    .in0(how_much), .in1(multiplexer_5_out), .out(multiplexer_4_out), .sel(comparator_2_eq));  // open: en
  Multiplexer #(.width(16)) multiplexer_5 (
    .in0({16{1'b0}}), .out(multiplexer_5_out), .sel(comparator_2_eq));  // open: in1, en
  and and_1 (from_break, from_signal, comparator_3_gt);
  or or_1 (or_1_out, comparator_3_eq, comparator_3_lt);
  Transistor #(.\type ("n"), .width(16)) transistor_2 (.in(register_1_q), .out(address_bus), .gate(from_break));
  Register #(.width(16)) register_2 (.D(multiplexer_2_out), .Q(from), .clk(clock));  // open: en, clr
  Register #(.width(16)) register_3 (.D(multiplexer_4_out), .Q(how_much), .clk(clock));  // open: en, clr
  Comparator #(.width(16), .mode("unsigned")) comparator_4 (
    .a({16{1'b0}}), .b(how_much), .eq(comparator_4_eq));  // open: gt, lt
  not not_1 (from_signal, comparator_4_eq);
  Pull_Resistor pull_resistor_2 (.node(pull_resistor_2_node));
  Transistor #(.\type ("n")) transistor_3 (.in(or_1_out), .out(pull_resistor_2_node), .gate(from_signal));
  Transistor transistor_4 (.in(pull_resistor_2_node), .out(transistor_4_out), .gate(block));
  Transistor #(.\type ("n"), .width(16)) transistor_5 (.in(16'hfc1c), .out(address_bus), .gate(transistor_4_out));
  Pull_Resistor pull_resistor_3 (.node(transistor_4_out));
  Transistor #(.\type ("n"), .width(16)) transistor_6 (
    .in(data_bus), .out({transistor_6_out, ext_data}), .gate(from_break));
  Transistor #(.\type ("n")) transistor_7 (.in(from_signal), .out(\break ), .gate(from_signal));
  Transistor #(.\type ("n"), .width(16)) transistor_8 (.in({16{1'b0}}), .out(data_bus), .gate(transistor_4_out));
  Transistor #(.\type ("n")) transistor_9 (.in(1'b1), .out(telnet), .gate(transistor_4_out));

  assign address_bus_2 = address_bus;
  assign data_bus_2 = data_bus;
endmodule

module key (
  input  in_1,
  output out_2
);

  wire transistor_1_out, xor_1_out;

  Transistor #(.\type ("n")) transistor_1 (.in(transistor_1_out), .out(transistor_1_out), .gate(in_1));
  Transistor transistor_2 (.in(xor_1_out), .out(transistor_1_out), .gate(in_1));
  Multiplexer multiplexer_1 (.in0(out_2), .in1(transistor_1_out), .out(out_2), .sel(in_1));  // open: en
  Pull_Resistor pull_resistor_1 (.node(out_2));
  xor xor_1 (xor_1_out, 1'b1, out_2);
endmodule

module inc (
  input  [7:0] in_1,
  output [7:0] out_2
);

  Adder adder_1 (.a(8'h1), .b(in_1), .out(out_2));  // open: cin, cout
endmodule

module print_num (
  input  [7:0] break_point,
  input  [15:0] start_add,
  input  [7:0] _1_num,
  input  [7:0] _2_num,
  input  [7:0] _3_num,
  input  [7:0] _4_num,
  input  [15:0] data_bus,
  input  [15:0] address_bus,
  input  clock,
  output [7:0] exit_data,
  output [7:0] out_11,
  output [15:0] out_12,
  output sp_break,
  output [7:0] address,
  output tag_1
);

  wire comparator_1_eq, comparator_2_lt, comparator_4_eq, comparator_5_eq, comparator_6_eq, comparator_7_eq,
       not_1_out, sig, sp_sign;
  wire [7:0] divider_1_rem, inc_1_out_2, transistor_3_out;
  wire [15:0] divider_1_out, multiplexer_1_out, multiplexer_2_out, transistor_1_out;

  Comparator #(.width(16), .mode("unsigned")) comparator_1 (
    .a(out_12), .b({16{1'b0}}), .eq(comparator_1_eq));  // open: gt, lt
  Comparator comparator_2 (.a(address), .b(break_point), .lt(comparator_2_lt));  // open: gt, eq
  Comparator #(.width(16), .mode("unsigned")) comparator_3 (.a(address_bus), .b(start_add), .eq(sig));  // open: gt, lt
  Pull_Resistor pull_resistor_1 (.node(sig));
  not not_1 (not_1_out, comparator_1_eq);
  and and_1 (sp_break, not_1_out, comparator_2_lt);
  Multiplexer #(.width(16)) multiplexer_1 (
    .in0(out_12), .in1(transistor_1_out), .out(multiplexer_1_out), .sel(tag_1));  // open: en
  Transistor #(.width(16)) transistor_1 (.in(transistor_1_out), .out(transistor_1_out), .gate(tag_1));
  Multiplexer #(.width(16)) multiplexer_2 (
    .in0(multiplexer_1_out), .in1(data_bus), .out(multiplexer_2_out), .sel(sig));  // open: en
  Register #(.width(16)) register_1 (.D(multiplexer_2_out), .Q(out_12), .clk(clock));  // open: en, clr
  Comparator #(.mode("unsigned")) comparator_4 (
    .a(address), .b(_1_num), .eq(comparator_4_eq), .lt(sp_sign));  // open: gt
  Comparator #(.mode("unsigned")) comparator_5 (.a(address), .b(_2_num), .eq(comparator_5_eq));  // open: gt, lt
  Comparator #(.mode("unsigned")) comparator_6 (.a(address), .b(_3_num), .eq(comparator_6_eq));  // open: gt, lt
  Comparator #(.mode("unsigned")) comparator_7 (.a(address), .b(_4_num), .eq(comparator_7_eq));  // open: gt, lt
  Transistor #(.\type ("n"), .width(16)) transistor_2 (.in(divider_1_out), .out(transistor_1_out), .gate(tag_1));
  Divider #(.width(16)) divider_1 (
    .a(out_12), .b(16'ha), .out(divider_1_out), .rem({divider_1_rem, exit_data}));  // open: upper
  or or_1 (tag_1, comparator_4_eq, comparator_5_eq, comparator_6_eq, comparator_7_eq);
  Transistor #(.\type ("n"), .width(8)) transistor_3 (.in(inc_1_out_2), .out(transistor_3_out), .gate(sp_break));
  inc inc_1 (.in_1(address), .out_2(inc_1_out_2));
  Register register_2 (.D(transistor_3_out), .Q(address), .clk(clock), .clr(sig));  // open: en

  assign out_11 = address;

  // Other names for the same wires on the sheet: ext_data_1[7:0] = exit_data; ad_1[7:0] = address
endmodule

module again_print_num (
  input  sp_break,
  input  [7:0] not_exit_data,
  input  [7:0] exit_data,
  input  tag_1,
  output [7:0] exit_data_2
);

  wire [7:0] adder_1_out, multiplexer_1_out;

  Adder adder_1 (.a(8'h30), .b(exit_data), .out(adder_1_out));  // open: cin, cout
  Multiplexer #(.width(8)) multiplexer_1 (
    .in0(not_exit_data), .in1(adder_1_out), .out(multiplexer_1_out), .sel(tag_1));  // open: en
  Transistor #(.\type ("n"), .width(8)) transistor_1 (.in(multiplexer_1_out), .out(exit_data_2), .gate(sp_break));
endmodule
