// Logisim project abudabi.circ as structural Verilog: 1 circuit, main circuit main
module main (
);

  wire cdm16_1_p1, cdm16_1_p3, clc, mem, not_1_out, read, word;
  wire [15:0] address_bus, cdm16_1_p9, cdm16_1_p10, data_bus;

  // Probe on cdm16_1_p1
  Clock clock_1 (.out(clc));
  // Probe on cdm16_1_p3
  // cdm16 cdm16_1: pin names not known; wires that end beside it: cdm16_1_p1, cdm16_1_p1, cdm16_1_p3, clc, mem, read, word, address_bus, cdm16_1_p9, cdm16_1_p10
  assign data_bus = not_1_out ? cdm16_1_p9 : 16'bz;  // Controlled_Buffer controlled_buffer_1
  not not_1 (not_1_out, read);
  assign cdm16_1_p10 = read ? data_bus : 16'bz;  // Controlled_Buffer controlled_buffer_2
  // Debugger debugger_1: pin names not known
  // RAM ram_1: pin names not known; wires that end beside it: address_bus, word, mem, clc, read, data_bus
endmodule
