// Logisim project tennis_circ.circ as structural Verilog
module main (
  input  [4:0] in_1
);

  wire cdm16_1_p1, cdm16_1_p2, cdm16_1_p4, cdm16_1_p5, cdm16_1_p6, cdm16_1_p7, cdm16_1_p8, cdm16_1_p9, clock,
       comparator_1_eq, comparator_2_eq, comparator_2_gt, comparator_3_eq, comparator_3_lt, comparator_4_eq,
       comparator_4_gt, comparator_5_eq, comparator_5_lt, comparator_6_gt, comparator_7_eq, comparator_8_eq,
       comparator_9_eq, comparator_10_eq, comparator_11_eq, comparator_12_eq, crash_left_bat, D, d_ff_1_q,
       mem, multiplexer_1_out, multiplexer_11_out, multiplexer_16_out, multiplexer_17_out,
       multiplexer_18_out, multiplexer_19_out, not_1_out, not_2_out, not_3_out, not_4_out, on_off, or_1_out,
       or_2_out, or_3_out, or_4_out, or_7_out, ram_1_p5, read, S_out, start, t_ff_1_q, t_ff_2_q, t_ff_3_q,
       t_ff_4_q, U, vx_change, vy_change, word;
  wire [2:0] count_dt, undriven, x_8, y_8;
  wire [4:0] adder_4_out, adder_5_out, adder_6_out, right_bat, video_1_ball_x_2, video_1_ball_y_2,
       video_1_chip_id_2, video_1_left_bat_y_2, video_1_right_bat_y_2, video_2_ball_x_2, video_2_ball_y_2,
       video_2_chip_id_2, video_2_left_bat_y_2, video_2_right_bat_y_2, video_3_ball_x_2, video_3_ball_y_2,
       video_3_chip_id_2, video_3_left_bat_y_2, video_3_right_bat_y_2, x_5, y_5;
  wire [7:0] adder_1_out, adder_2_out, adder_3_out, left_bat_y, multiplexer_2_out, multiplexer_3_out,
       multiplexer_5_out, multiplexer_6_out, multiplexer_8_out, multiplexer_9_out, multiplexer_10_out,
       multiplexer_12_out, multiplexer_14_out, neg_vx, neg_vy, subtractor_1_out, vx, vy;
  wire [15:0] address_bus, cdm16_1_p15, cdm16_1_p16, data_bus, multiplexer_4_out, multiplexer_7_out,
       multiplexer_15_out, pc, ram_1_p7, register_1_q;
  wire [31:0] video_1_out_6, video_1_out_7, video_1_out_8, video_1_out_9, video_1_out_10, video_1_out_11,
       video_1_out_12, video_1_out_13, video_2_out_6, video_2_out_7, video_2_out_8, video_2_out_9,
       video_2_out_10, video_2_out_11, video_2_out_12, video_2_out_13, video_3_out_6, video_3_out_7,
       video_3_out_8, video_3_out_9, video_3_out_10, video_3_out_11, video_3_out_12, video_3_out_13,
       video_4_out_6, video_4_out_7, video_4_out_8, video_4_out_9, video_4_out_10, video_4_out_11,
       video_4_out_12, video_4_out_13;

  // Probe on cdm16_1_p4
  // Probe on cdm16_1_p2
  // Probe on cdm16_1_p1
  Multiplexer multiplexer_1 (.in1(clock), .out(multiplexer_1_out), .sel(1'b1), .en(on_off));  // open: in0
  Clock clock_1 (.out(clock));
  // Probe on cdm16_1_p9
  // Probe on cdm16_1_p8
  // Probe on cdm16_1_p7
  // Probe on cdm16_1_p6
  // Probe on cdm16_1_p5
  // Probe on pc
  // cdm16 cdm16_1: pin names not known; wires that end beside it: cdm16_1_p1, cdm16_1_p2, multiplexer_1_out, cdm16_1_p4, cdm16_1_p5, cdm16_1_p6, cdm16_1_p7, cdm16_1_p8, cdm16_1_p9, pc, mem, read, word, address_bus, cdm16_1_p15, cdm16_1_p16
  Multiplexer #(.width(8)) multiplexer_2 (
    .in0(vy), .in1(neg_vy), .out(multiplexer_2_out), .sel(vy_change));  // open: en
  Comparator #(.width(16)) comparator_1 (.a(address_bus), .b(16'hffa), .eq(comparator_1_eq));  // open: gt, lt
  assign data_bus = not_1_out ? cdm16_1_p15 : 16'bz;  // Controlled_Buffer controlled_buffer_1
  not not_1 (not_1_out, read);
  assign cdm16_1_p16 = read ? data_bus : 16'bz;  // Controlled_Buffer controlled_buffer_2
  Multiplexer #(.width(8)) multiplexer_3 (
    .in0(vx), .in1(neg_vx), .out(multiplexer_3_out), .sel(vx_change));  // open: en
  Multiplexer #(.width(16), .enable("false")) multiplexer_4 (
    .in0({register_1_q[15:8], right_bat, register_1_q[2:0]}), .in1(data_bus), .out(multiplexer_4_out),
    .sel(comparator_1_eq));
  Register #(.width(16)) register_1 (
    .D(multiplexer_4_out), .Q({register_1_q[15:8], right_bat, register_1_q[2:0]}), .clk(clock));  // open: en, clr
  Multiplexer #(.width(8)) multiplexer_5 (
    .in0(8'hfe), .in1(multiplexer_3_out), .out(multiplexer_5_out), .sel(t_ff_1_q));  // open: en
  T_Flip_Flop t_ff_1 (.clk(clock), .Q(t_ff_1_q), .preset(start), .en(1'b1));  // open: T, Qn, reset
  Multiplexer #(.width(8)) multiplexer_6 (
    .in0(8'h2), .in1(multiplexer_2_out), .out(multiplexer_6_out), .sel(t_ff_2_q));  // open: en
  T_Flip_Flop t_ff_2 (.clk(clock), .Q(t_ff_2_q), .preset(start), .en(1'b1));  // open: T, Qn, reset
  Multiplexer #(.select(3), .width(16)) multiplexer_7 (
    .in1(16'hff0), .in2(16'hff2), .in3(16'hff4), .in4(16'hff6), .in5(16'hff8), .in6(16'hffa),
    .in7(address_bus), .out(multiplexer_7_out), .sel(count_dt));  // open: in0, en
  // Debugger debugger_1: pin names not known
  Register u_vx (.D(multiplexer_5_out), .Q(vx), .clk(clock));  // open: en, clr
  Register u_vy (.D(multiplexer_6_out), .Q(vy), .clk(clock));  // open: en, clr
  // Probe on vx
  Multiplexer #(.width(8), .enable("false")) multiplexer_8 (
    .in0(vx), .in1(neg_vx), .out(multiplexer_8_out), .sel(vx_change));
  Multiplexer #(.width(8)) multiplexer_9 (
    .in0(vy), .in1(neg_vy), .out(multiplexer_9_out), .sel(vy_change));  // open: en
  not not_2 (not_2_out, on_off);
  Adder adder_1 (.a({x_5, x_8}), .b(multiplexer_8_out), .out(adder_1_out));  // open: cin, cout
  Multiplexer #(.width(8)) multiplexer_10 (
    .in0(8'h7f), .in1(adder_1_out), .out(multiplexer_10_out), .sel(t_ff_3_q));  // open: en
  T_Flip_Flop t_ff_3 (.clk(clock), .Q(t_ff_3_q), .preset(start), .en(1'b1));  // open: T, Qn, reset
  Adder adder_2 (.a({y_5, y_8}), .b(multiplexer_9_out), .out(adder_2_out));  // open: cin, cout
  T_Flip_Flop t_ff_4 (.clk(clock), .Q(t_ff_4_q), .preset(start), .en(1'b1));  // open: T, Qn, reset
  Multiplexer #(.select(3)) multiplexer_11 (
    .in0(not_2_out), .in1(not_2_out), .in2(not_2_out), .in3(not_2_out), .in4(not_2_out), .in5(not_2_out),
    .in6(not_2_out), .in7(mem), .out(multiplexer_11_out), .sel(count_dt));  // open: en
  Adder adder_3 (.a(left_bat_y), .b(8'h3), .out(adder_3_out));  // open: cin, cout
  Subtractor subtractor_1 (.a(left_bat_y), .b(8'h3), .out(subtractor_1_out));  // open: bin, bout
  Register x (.D(multiplexer_10_out), .Q({x_5, x_8}), .clk(clock));  // open: en, clr
  Register y (.D(multiplexer_12_out), .Q({y_5, y_8}), .clk(clock));  // open: en, clr
  Multiplexer #(.width(8)) multiplexer_12 (
    .in0(8'h7f), .in1(adder_2_out), .out(multiplexer_12_out), .sel(t_ff_4_q));  // open: en
  // RAM ram_1: pin names not known; wires that end beside it: multiplexer_7_out, word, multiplexer_11_out, clock, ram_1_p5, read, ram_1_p7
  Multiplexer #(.select(3)) multiplexer_13 (
    .in0(on_off), .in1(on_off), .in2(on_off), .in3(on_off), .in4(on_off), .in5(on_off), .in6(on_off),
    .in7(read), .out(ram_1_p5), .sel(count_dt));  // open: en
  Multiplexer #(.select(2), .width(8)) multiplexer_14 (
    .in0(left_bat_y), .in1(adder_3_out), .in2(subtractor_1_out), .out(multiplexer_14_out), .sel({D, U}));  // open: in3, en
  Register register_2 (.D(multiplexer_14_out), .Q(left_bat_y), .clk(clock));  // open: en, clr
  assign ram_1_p7 = not_3_out ? multiplexer_15_out : 16'bz;  // Controlled_Buffer controlled_buffer_3
  not not_3 (not_3_out, on_off);
  assign data_bus = on_off ? ram_1_p7 : 16'bz;  // Controlled_Buffer controlled_buffer_4
  Button S (.out(S_out));
  Button u_U (.out(U));
  Button u_D (.out(D));
  // Probe on left_bat_y[7:3]
  T_Flip_Flop t_ff_5 (.clk(clock), .Q(start), .preset(S_out), .en(1'b1));  // open: T, Qn, reset
  DotMatrix #(.matrixcols(32), .matrixrows(32)) dotmatrix_1 (
    .col0(video_1_out_6), .col1(video_1_out_7), .col2(video_1_out_8), .col3(video_1_out_9),
    .col4(video_1_out_10), .col5(video_1_out_11), .col6(video_1_out_12), .col7(video_1_out_13),
    .col8(video_2_out_6), .col9(video_2_out_7), .col10(video_2_out_8), .col11(video_2_out_9),
    .col12(video_2_out_10), .col13(video_2_out_11), .col14(video_2_out_12), .col15(video_2_out_13),
    .col16(video_3_out_6), .col17(video_3_out_7), .col18(video_3_out_8), .col19(video_3_out_9),
    .col20(video_3_out_10), .col21(video_3_out_11), .col22(video_3_out_12), .col23(video_3_out_13),
    .col24(video_4_out_6), .col25(video_4_out_7), .col26(video_4_out_8), .col27(video_4_out_9),
    .col28(video_4_out_10), .col29(video_4_out_11), .col30(video_4_out_12), .col31(video_4_out_13));
  Comparator #(.mode("unsigned")) comparator_2 (
    .a({x_5, x_8}), .b(8'hfe), .gt(comparator_2_gt), .eq(comparator_2_eq));  // open: lt
  Comparator #(.mode("unsigned")) comparator_3 (
    .a({x_5, x_8}), .b(8'h1), .eq(comparator_3_eq), .lt(comparator_3_lt));  // open: gt
  // Probe on neg_vx
  Negator negator_1 (.in(vx), .out(neg_vx));
  Comparator #(.mode("unsigned")) comparator_4 (
    .a({y_5, y_8}), .b(8'hfe), .gt(comparator_4_gt), .eq(comparator_4_eq));  // open: lt
  Comparator #(.mode("unsigned")) comparator_5 (
    .a({y_5, y_8}), .b(8'h1), .eq(comparator_5_eq), .lt(comparator_5_lt));  // open: gt
  // Probe on neg_vy
  Negator negator_2 (.in(vy), .out(neg_vy));
  // Probe on {{8{1'b0}}, x_5, x_8}
  video video_1 (
    .Chip_ID_2(video_1_chip_id_2), .Ball_X_2(video_1_ball_x_2), .Ball_Y_2(video_1_ball_y_2),
    .left_bat_Y_2(video_1_left_bat_y_2), .right_bat_Y_2(video_1_right_bat_y_2), .out_6(video_1_out_6),
    .out_7(video_1_out_7), .out_8(video_1_out_8), .out_9(video_1_out_9), .out_10(video_1_out_10),
    .out_11(video_1_out_11), .out_12(video_1_out_12), .out_13(video_1_out_13), .Chip_ID(in_1), .Ball_X(x_5),
    .Ball_Y(y_5), .left_bat_Y(left_bat_y[7:3]), .right_bat_Y(right_bat));
  or or_1 (or_1_out, comparator_2_gt, comparator_2_eq);
  or or_2 (or_2_out, comparator_3_eq, comparator_3_lt);
  or or_3 (or_3_out, comparator_4_gt, comparator_4_eq);
  or or_4 (or_4_out, comparator_5_eq, comparator_5_lt);
  Multiplexer #(.select(3), .width(16)) multiplexer_15 (
    .in1({{8{1'b0}}, x_5, x_8}), .in2({{8{1'b0}}, y_5, y_8}), .in3({{8{1'b0}}, vx}), .in4({{8{1'b0}}, vy}),
    .in5({{8{1'b0}}, left_bat_y}), .in6({16{1'b0}}), .in7(data_bus), .out(multiplexer_15_out), .sel(count_dt));  // open: in0, en
  // Probe on count_dt
  video video_2 (
    .Chip_ID_2(video_2_chip_id_2), .Ball_X_2(video_2_ball_x_2), .Ball_Y_2(video_2_ball_y_2),
    .left_bat_Y_2(video_2_left_bat_y_2), .right_bat_Y_2(video_2_right_bat_y_2), .out_6(video_2_out_6),
    .out_7(video_2_out_7), .out_8(video_2_out_8), .out_9(video_2_out_9), .out_10(video_2_out_10),
    .out_11(video_2_out_11), .out_12(video_2_out_12), .out_13(video_2_out_13), .Chip_ID(video_1_chip_id_2),
    .Ball_X(video_1_ball_x_2), .Ball_Y(video_1_ball_y_2), .left_bat_Y(video_1_left_bat_y_2),
    .right_bat_Y(video_1_right_bat_y_2));
  or or_5 (vx_change, or_1_out, crash_left_bat, or_2_out);
  or or_6 (vy_change, or_3_out, or_4_out);
  video video_3 (
    .Chip_ID_2(video_3_chip_id_2), .Ball_X_2(video_3_ball_x_2), .Ball_Y_2(video_3_ball_y_2),
    .left_bat_Y_2(video_3_left_bat_y_2), .right_bat_Y_2(video_3_right_bat_y_2), .out_6(video_3_out_6),
    .out_7(video_3_out_7), .out_8(video_3_out_8), .out_9(video_3_out_9), .out_10(video_3_out_10),
    .out_11(video_3_out_11), .out_12(video_3_out_12), .out_13(video_3_out_13), .Chip_ID(video_2_chip_id_2),
    .Ball_X(video_2_ball_x_2), .Ball_Y(video_2_ball_y_2), .left_bat_Y(video_2_left_bat_y_2),
    .right_bat_Y(video_2_right_bat_y_2));
  Multiplexer multiplexer_16 (.in1(clock), .out(multiplexer_16_out), .sel(comparator_6_gt));  // open: in0, en
  Comparator comparator_6 (.a(vx), .b({8{1'b0}}), .gt(comparator_6_gt));  // open: eq, lt
  video video_4 (
    .out_6(video_4_out_6), .out_7(video_4_out_7), .out_8(video_4_out_8), .out_9(video_4_out_9),
    .out_10(video_4_out_10), .out_11(video_4_out_11), .out_12(video_4_out_12), .out_13(video_4_out_13),
    .Chip_ID(video_3_chip_id_2), .Ball_X(video_3_ball_x_2), .Ball_Y(video_3_ball_y_2),
    .left_bat_Y(video_3_left_bat_y_2), .right_bat_Y(video_3_right_bat_y_2));  // open: Chip_ID_2, Ball_X_2, Ball_Y_2, left_bat_Y_2, right_bat_Y_2
  // Probe on y_5
  Comparator #(.width(5)) comparator_7 (.a(y_5), .b(left_bat_y[7:3]), .eq(comparator_7_eq));  // open: gt, lt
  Comparator #(.width(5)) comparator_8 (.a(y_5), .b(adder_4_out), .eq(comparator_8_eq));  // open: gt, lt
  Adder #(.width(5)) adder_4 (.a(left_bat_y[7:3]), .b(5'b00001), .out(adder_4_out));  // open: cin, cout
  Comparator #(.width(5)) comparator_9 (.a(y_5), .b(adder_5_out), .eq(comparator_9_eq));  // open: gt, lt
  Adder #(.width(5)) adder_5 (.a(left_bat_y[7:3]), .b(5'b00010), .out(adder_5_out));  // open: cin, cout
  Adder #(.width(5)) adder_6 (.a(left_bat_y[7:3]), .b(5'b00011), .out(adder_6_out));  // open: cin, cout
  D_Flip_Flop d_ff_1 (.clk(on_off), .Q(d_ff_1_q), .preset(on_off), .reset(multiplexer_18_out));  // open: D, Qn, en
  Comparator #(.width(5)) comparator_10 (.a(y_5), .b(adder_6_out), .eq(comparator_10_eq));  // open: gt, lt
  Multiplexer multiplexer_17 (
    .in0(multiplexer_16_out), .in1(1'b0), .out(multiplexer_17_out), .sel(d_ff_1_q));  // open: en
  Multiplexer #(.enable("false")) multiplexer_18 (
    .in1(1'b1), .out(multiplexer_18_out), .sel(comparator_11_eq));  // open: in0
  Comparator #(.width(16)) comparator_11 (.a(pc), .b(16'h120), .eq(comparator_11_eq));  // open: gt, lt
  Comparator #(.width(5)) comparator_12 (.a(x_5), .b(5'b00010), .eq(comparator_12_eq));  // open: gt, lt
  or or_7 (or_7_out, comparator_7_eq, comparator_8_eq, comparator_10_eq, comparator_9_eq);
  Counter #(.width(3), .max('h7)) counter_1 (
    .Q(count_dt), .clk(multiplexer_17_out), .clr(multiplexer_19_out));  // open: load, D, count, carry
  Multiplexer multiplexer_19 (.in1(not_4_out), .out(multiplexer_19_out), .sel(multiplexer_18_out));  // open: in0, en
  not not_4 (not_4_out, multiplexer_18_out);
  and and_1 (crash_left_bat, comparator_12_eq, or_7_out);
  Comparator #(.width(3)) comparator_13 (.a(count_dt), .b(undriven));  // open: gt, eq, lt
  Comparator #(.width(3)) comparator_14 (.a(count_dt), .b(3'b111), .eq(on_off));  // open: gt, lt

  // Other names for the same wires on the sheet: y_8[7:3] = y_5; x_8[7:3] = x_5; left_bat_y_5[4:0] = left_bat_y[7:3]
endmodule

module video (
  input  [4:0] Chip_ID,
  input  [4:0] Ball_X,
  input  [4:0] Ball_Y,
  input  [4:0] left_bat_Y,
  input  [4:0] right_bat_Y,
  output [31:0] out_6,
  output [31:0] out_7,
  output [31:0] out_8,
  output [31:0] out_9,
  output [31:0] out_10,
  output [31:0] out_11,
  output [31:0] out_12,
  output [31:0] out_13,
  output [4:0] Chip_ID_2,
  output [4:0] Ball_X_2,
  output [4:0] Ball_Y_2,
  output [4:0] left_bat_Y_2,
  output [4:0] right_bat_Y_2
);

  wire comparator_1_eq, comparator_2_eq, comparator_3_eq, comparator_4_eq, comparator_5_eq, comparator_6_eq,
       comparator_7_eq, comparator_8_eq, comparator_9_eq, comparator_10_eq, not_1_out;
  wire [4:0] id_1, id_2, id_3, id_4, id_5, id_6, id_7, video_chip_1_out_7, video_chip_1_out_8,
       video_chip_1_out_9, video_chip_1_out_10, video_chip_2_out_7, video_chip_2_out_8, video_chip_2_out_9,
       video_chip_2_out_10, video_chip_3_out_7, video_chip_3_out_8, video_chip_3_out_9, video_chip_3_out_10,
       video_chip_4_out_7, video_chip_4_out_8, video_chip_4_out_9, video_chip_4_out_10, video_chip_5_out_7,
       video_chip_5_out_8, video_chip_5_out_9, video_chip_5_out_10, video_chip_6_out_7, video_chip_6_out_8,
       video_chip_6_out_9, video_chip_6_out_10, video_chip_7_out_7, video_chip_7_out_8, video_chip_7_out_9,
       video_chip_7_out_10;
  wire [31:0] BALLS_OUT, l_bat_print, multiplexer_3_out, multiplexer_4_out, multiplexer_7_out,
       multiplexer_8_out, r_bat_print;

  Multiplexer #(.width(32)) multiplexer_1 (
    .in0({32{1'b0}}), .in1(BALLS_OUT), .out(out_6), .sel(comparator_1_eq));  // open: en
  Comparator #(.width(5)) comparator_1 (.a(Chip_ID), .b(Ball_X), .eq(comparator_1_eq));  // open: gt, lt
  Multiplexer #(.width(32)) multiplexer_2 (
    .in0({32{1'b0}}), .in1(BALLS_OUT), .out(out_7), .sel(comparator_2_eq));  // open: en
  Comparator #(.width(5)) comparator_2 (.a(id_1), .b(Ball_X), .eq(comparator_2_eq));  // open: gt, lt
  Multiplexer #(.width(32)) multiplexer_3 (
    .in0({32{1'b0}}), .in1(l_bat_print), .out(multiplexer_3_out), .sel(comparator_3_eq));  // open: en
  Comparator #(.width(5)) comparator_3 (.a(Chip_ID), .b({5{1'b0}}), .eq(comparator_3_eq));  // open: gt, lt
  assign out_8 = multiplexer_3_out | multiplexer_4_out;  // OR_Gate or_1, 32 bits wide
  Multiplexer #(.width(32)) multiplexer_4 (
    .in0({32{1'b0}}), .in1(BALLS_OUT), .out(multiplexer_4_out), .sel(comparator_4_eq));  // open: en
  Comparator #(.width(5)) comparator_4 (.a(id_2), .b(Ball_X), .eq(comparator_4_eq));  // open: gt, lt
  video_chip video_chip_1 (
    .Chip_id(Chip_ID), .Ball_X(Ball_X), .Ball_Y(Ball_Y), .left_bat_X(left_bat_Y), .right_bat_Y(right_bat_Y),
    .out_6(id_1), .out_7(video_chip_1_out_7), .out_8(video_chip_1_out_8), .out_9(video_chip_1_out_9),
    .out_10(video_chip_1_out_10));
  video_chip video_chip_2 (
    .Chip_id(id_1), .Ball_X(video_chip_1_out_7), .Ball_Y(video_chip_1_out_8),
    .left_bat_X(video_chip_1_out_9), .right_bat_Y(video_chip_1_out_10), .out_6(id_2),
    .out_7(video_chip_2_out_7), .out_8(video_chip_2_out_8), .out_9(video_chip_2_out_9),
    .out_10(video_chip_2_out_10));
  video_chip video_chip_3 (
    .Chip_id(id_2), .Ball_X(video_chip_2_out_7), .Ball_Y(video_chip_2_out_8),
    .left_bat_X(video_chip_2_out_9), .right_bat_Y(video_chip_2_out_10), .out_6(id_3),
    .out_7(video_chip_3_out_7), .out_8(video_chip_3_out_8), .out_9(video_chip_3_out_9),
    .out_10(video_chip_3_out_10));
  Multiplexer #(.width(32)) multiplexer_5 (
    .in0({32{1'b0}}), .in1(BALLS_OUT), .out(out_9), .sel(comparator_5_eq));  // open: en
  Comparator #(.width(5)) comparator_5 (.a(id_3), .b(Ball_X), .eq(comparator_5_eq));  // open: gt, lt
  video_chip video_chip_4 (
    .Chip_id(id_3), .Ball_X(video_chip_3_out_7), .Ball_Y(video_chip_3_out_8),
    .left_bat_X(video_chip_3_out_9), .right_bat_Y(video_chip_3_out_10), .out_6(id_4),
    .out_7(video_chip_4_out_7), .out_8(video_chip_4_out_8), .out_9(video_chip_4_out_9),
    .out_10(video_chip_4_out_10));
  Shifter #(.width(32)) shifter_1 (.in(32'hf), .\dist (left_bat_Y), .out(l_bat_print));
  Shifter #(.width(32)) shifter_2 (.in(32'hf), .\dist (right_bat_Y), .out(r_bat_print));
  Multiplexer #(.width(32)) multiplexer_6 (
    .in0({32{1'b0}}), .in1(BALLS_OUT), .out(out_10), .sel(comparator_6_eq));  // open: en
  Comparator #(.width(5)) comparator_6 (.a(id_4), .b(Ball_X), .eq(comparator_6_eq));  // open: gt, lt
  video_chip video_chip_5 (
    .Chip_id(id_4), .Ball_X(video_chip_4_out_7), .Ball_Y(video_chip_4_out_8),
    .left_bat_X(video_chip_4_out_9), .right_bat_Y(video_chip_4_out_10), .out_6(id_5),
    .out_7(video_chip_5_out_7), .out_8(video_chip_5_out_8), .out_9(video_chip_5_out_9),
    .out_10(video_chip_5_out_10));
  video_chip video_chip_6 (
    .Chip_id(id_5), .Ball_X(video_chip_5_out_7), .Ball_Y(video_chip_5_out_8),
    .left_bat_X(video_chip_5_out_9), .right_bat_Y(video_chip_5_out_10), .out_6(id_6),
    .out_7(video_chip_6_out_7), .out_8(video_chip_6_out_8), .out_9(video_chip_6_out_9),
    .out_10(video_chip_6_out_10));
  video_chip video_chip_7 (
    .Chip_id(id_6), .Ball_X(video_chip_6_out_7), .Ball_Y(video_chip_6_out_8),
    .left_bat_X(video_chip_6_out_9), .right_bat_Y(video_chip_6_out_10), .out_6(id_7),
    .out_7(video_chip_7_out_7), .out_8(video_chip_7_out_8), .out_9(video_chip_7_out_9),
    .out_10(video_chip_7_out_10));
  assign out_11 = multiplexer_8_out | multiplexer_7_out;  // OR_Gate or_2, 32 bits wide
  Multiplexer #(.width(32)) multiplexer_7 (
    .in0({32{1'b0}}), .in1(r_bat_print), .out(multiplexer_7_out), .sel(comparator_8_eq));  // open: en
  Multiplexer #(.width(32)) multiplexer_8 (
    .in0({32{1'b0}}), .in1(BALLS_OUT), .out(multiplexer_8_out), .sel(comparator_7_eq));  // open: en
  Comparator #(.width(5)) comparator_7 (.a(id_5), .b(Ball_X), .eq(comparator_7_eq));  // open: gt, lt
  video_chip video_chip_8 (
    .Chip_id(id_7), .Ball_X(video_chip_7_out_7), .Ball_Y(video_chip_7_out_8),
    .left_bat_X(video_chip_7_out_9), .right_bat_Y(video_chip_7_out_10), .out_6(Chip_ID_2), .out_7(Ball_X_2),
    .out_8(Ball_Y_2), .out_9(left_bat_Y_2), .out_10(right_bat_Y_2));
  Shifter #(.width(32)) shifter_3 (.in(32'h1), .\dist (Ball_Y), .out(BALLS_OUT));
  Comparator #(.width(5)) comparator_8 (.a({5{1'b1}}), .b(id_7), .eq(comparator_8_eq));  // open: gt, lt
  Multiplexer #(.width(32)) multiplexer_9 (
    .in0({32{1'b0}}), .in1(BALLS_OUT), .out(out_12), .sel(comparator_9_eq));  // open: en
  Comparator #(.width(5)) comparator_9 (.a(id_6), .b(Ball_X), .eq(comparator_9_eq));  // open: gt, lt
  // NOT_Gate not_1 has open pins: in=open, out=not_1_out
  Multiplexer #(.width(32)) multiplexer_10 (
    .in0({32{1'b0}}), .in1(BALLS_OUT), .out(out_13), .sel(comparator_10_eq));  // open: en
  Comparator #(.width(5)) comparator_10 (.a(id_7), .b(Ball_X), .eq(comparator_10_eq));  // open: gt, lt

  // Other names for the same wires on the sheet: id_0[4:0] = Chip_ID; id_out[4:0] = Chip_ID_2;
  //   l_bat[4:0] = left_bat_Y; l_bat_out[4:0] = left_bat_Y_2; r_bat[4:0] = right_bat_Y;
  //   r_bat_out[4:0] = right_bat_Y_2; x[4:0] = Ball_X; x_out[4:0] = Ball_X_2; y[4:0] = Ball_Y; y_out[4:0] = Ball_Y_2

  // Notes on the sheet:
  //   0
  //   1
  //   2
  //   3
  //   4
  //   5
  //   6
  //   7
endmodule

module video_chip (
  input  [4:0] Chip_id,
  input  [4:0] Ball_X,
  input  [4:0] Ball_Y,
  input  [4:0] left_bat_X,
  input  [4:0] right_bat_Y,
  output [4:0] out_6,
  output [4:0] out_7,
  output [4:0] out_8,
  output [4:0] out_9,
  output [4:0] out_10
);

  Adder #(.width(5)) adder_1 (.a(5'b00001), .b(Chip_id), .out(out_6));  // open: cin, cout

  assign out_7 = Ball_X;
  assign out_8 = Ball_Y;
  assign out_9 = left_bat_X;
  assign out_10 = right_bat_Y;
endmodule
